// Logisim project 数字逻辑实验.circ as structural Verilog: 26 circuits, main circuit main
module main (
  input  A,
  input  B,
  input  cc,
  input  A_2,
  input  B_2,
  input  C,
  input  in_7,
  input  in_8,
  input  in_9,
  input  in_10,
  input  in_11
);

  wire and_1_out, and_2_out, and_3_out, n74ls00_1_out_9, n74ls00_1_out_11, n74ls00_1_out_12, nand_1_out,
       nand_2_out, nand_3_out, nand_4_out, nand_5_out, nand_6_out, nand_7_out, not_1_out, not_2_out,
       not_3_out, not_4_out, not_5_out, not_6_out, not_7_out, not_8_out, or_1_out, undriven, undriven_2,
       undriven_3, undriven_4, undriven_5, undriven_6, xor_1_out, xor_2_out;

  _74LS00 u_74ls00_1 (
    .in_1(A_2), .in_3(B_2), .out_9(n74ls00_1_out_9), .in_5(C), .in_7(A_2), .out_11(n74ls00_1_out_11),
    .in_6(C), .in_8(B_2), .out_12(n74ls00_1_out_12));  // open: in_2, in_4, out_10
  _74LS10 u_74ls10_1 (
    .in_1(n74ls00_1_out_9), .in_2(n74ls00_1_out_11), .in_3(n74ls00_1_out_12), .out_10(in_9));  // open: in_4, in_6, in_8, out_11, in_5, in_7, in_9, out_12
  point u_A ();  // open: A, B, cc, A0, A1, A2, D0, D1, D2, D3, D4, D5, D6, D7, S, C
  xor xor_1 (xor_1_out, A, B);
  and and_1 (and_1_out, A, B);
  and and_2 (and_2_out, A, cc);
  and and_3 (and_3_out, B, cc);
  not not_1 (not_1_out, undriven);
  not not_2 (not_2_out, undriven_2);
  not not_3 (not_3_out, undriven_3);
  not not_4 (not_4_out, undriven_4);
  not not_5 (not_5_out, in_11);
  not not_6 (not_6_out, in_10);
  xor xor_2 (xor_2_out, xor_1_out, cc);
  or or_1 (or_1_out, and_1_out, and_2_out, and_3_out);
  nand nand_1 (nand_1_out, in_7, in_8);
  LED led_1 (.in(nand_1_out));
  nand nand_2 (nand_2_out, undriven_5, undriven_6);
  nand nand_3 (nand_3_out, not_1_out, not_2_out);
  nand nand_4 (nand_4_out, not_3_out, not_4_out);
  nand nand_5 (nand_5_out, in_10, not_5_out);
  nand nand_6 (nand_6_out, in_11, not_6_out);
  LED S (.in(xor_2_out));
  LED u_C (.in(or_1_out));
  not not_7 (not_7_out, nand_2_out);
  not not_8 (not_8_out, nand_4_out);
  LED led_2 (.in(nand_7_out));
  nand nand_7 (nand_7_out, nand_5_out, nand_5_out, nand_6_out, nand_6_out);

  // Notes on the sheet:
  //   三人表决器
  //   A
  //   B
  //   cc
  //   S
  //   C
endmodule

module _74LS00 (
  input  in_1,
  input  in_2,
  input  in_3,
  input  in_4,
  input  in_5,
  input  in_6,
  input  in_7,
  input  in_8,
  output out_9,
  output out_10,
  output out_11,
  output out_12
);

  nand nand_1 (out_9, in_3, in_1);
  nand nand_2 (out_11, in_7, in_5);
  nand nand_3 (out_10, in_2, in_4);
  nand nand_4 (out_12, in_6, in_8);
endmodule

module _74LS08 (
  input  in_1,
  input  in_2,
  input  in_3,
  input  in_4,
  input  in_5,
  input  in_6,
  input  in_7,
  input  in_8,
  output out_9,
  output out_10,
  output out_11,
  output out_12
);

  and and_1 (out_9, in_3, in_1);
  and and_2 (out_11, in_7, in_5);
  and and_3 (out_10, in_2, in_4);
  and and_4 (out_12, in_6, in_8);
endmodule

module _74LS04 (
  input  in_1,
  input  in_2,
  input  in_3,
  input  in_4,
  input  in_5,
  input  in_6,
  output out_7,
  output out_8,
  output out_9,
  output out_10,
  output out_11,
  output out_12
);

  not not_1 (out_7, in_1);
  not not_2 (out_9, in_3);
  not not_3 (out_11, in_5);
  not not_4 (out_8, in_2);
  not not_5 (out_10, in_4);
  not not_6 (out_12, in_6);
endmodule

module _74LS10 (
  input  in_1,
  input  in_2,
  input  in_3,
  input  in_4,
  input  in_5,
  input  in_6,
  input  in_7,
  input  in_8,
  input  in_9,
  output out_10,
  output out_11,
  output out_12
);

  nand nand_1 (out_11, in_8, in_6, in_4);
  nand nand_2 (out_10, in_2, in_1, in_3);
  nand nand_3 (out_12, in_5, in_7, in_9);
endmodule

module _74LS20 (
  input  in_1,
  input  in_2,
  input  in_3,
  input  in_4,
  input  in_5,
  input  in_6,
  input  in_7,
  input  in_8,
  input  in_9,
  input  in_10,
  output out_11,
  output out_12
);

  nand nand_1 (out_11, in_9, in_7, in_3, in_1);
  nand nand_2 (out_12, in_2, in_4, in_8, in_10);
endmodule

module _74LS32 (
  input  in_1,
  input  in_2,
  input  in_3,
  input  in_4,
  input  in_5,
  input  in_6,
  input  in_7,
  input  in_8,
  output out_9,
  output out_10,
  output out_11,
  output out_12
);

  or or_1 (out_9, in_3, in_1);
  or or_2 (out_11, in_7, in_5);
  or or_3 (out_10, in_2, in_4);
  or or_4 (out_12, in_6, in_8);
endmodule

module _74LS86 (
  input  in_1,
  input  in_2,
  input  in_3,
  input  in_4,
  input  in_5,
  input  in_6,
  input  in_7,
  input  in_8,
  output out_9,
  output out_10,
  output out_11,
  output out_12
);

  xor xor_1 (out_9, in_3, in_1);
  xor xor_2 (out_11, in_7, in_5);
  xor xor_3 (out_10, in_2, in_4);
  xor xor_4 (out_12, in_6, in_8);
endmodule

module _74LS138 (
  input  in_1,
  input  in_2,
  input  in_3,
  input  in_4,
  input  in_5,
  input  in_6,
  output out_7,
  output out_8,
  output out_9,
  output out_10,
  output out_11,
  output out_12,
  output out_13,
  output out_14
);

  wire and_1_out, decoder_1_out0, decoder_1_out1, decoder_1_out2, decoder_1_out3, decoder_1_out4,
       decoder_1_out5, decoder_1_out6, decoder_1_out7;

  and and_1 (and_1_out, ~in_4, ~in_5, in_6);  // AND_Gate
  not not_1 (out_13, decoder_1_out7);
  Decoder #(.select(3), .disabled(0)) decoder_1 (
    .out0(decoder_1_out0), .out1(decoder_1_out1), .out2(decoder_1_out2), .out3(decoder_1_out3),
    .out4(decoder_1_out4), .out5(decoder_1_out5), .out6(decoder_1_out6), .out7(decoder_1_out7),
    .sel({in_3, in_2, in_1}), .en(and_1_out));
  not not_2 (out_7, decoder_1_out0);
  not not_3 (out_8, decoder_1_out1);
  not not_4 (out_9, decoder_1_out2);
  not not_5 (out_10, decoder_1_out3);
  not not_6 (out_11, decoder_1_out4);
  not not_7 (out_12, decoder_1_out5);
  not not_8 (out_14, decoder_1_out6);
endmodule

module point (
  input  A,
  input  B,
  input  cc,
  input  A0,
  input  A1,
  input  A2,
  input  D0,
  input  D1,
  input  D2,
  input  D3,
  input  D4,
  input  D5,
  input  D6,
  input  D7,
  output S,
  output C
);

  wire and_1_out, and_2_out, and_3_out, and_4_out, and_5_out, and_6_out, and_7_out, n7_1_f, not_1_out,
       not_2_out, not_3_out, not_4_out, not_5_out, not_6_out;

  not not_1 (not_1_out, A);
  not not_2 (not_2_out, B);
  not not_3 (not_3_out, A);
  not not_4 (not_4_out, cc);
  not not_5 (not_5_out, B);
  not not_6 (not_6_out, cc);
  and and_1 (and_1_out, B, cc);
  and and_2 (and_2_out, A, cc);
  and and_3 (and_3_out, A, B);
  and and_4 (and_4_out, not_1_out, not_2_out, cc);
  and and_5 (and_5_out, not_3_out, B, not_4_out);
  and and_6 (and_6_out, A, not_5_out, not_6_out);
  and and_7 (and_7_out, A, B, cc);
  or or_1 (C, and_1_out, and_2_out, and_3_out);
  or or_2 (S, and_4_out, and_5_out, and_6_out, and_7_out);
  _7 u_7_1 (
    .A0(A0), .A1(A1), .A2(A2), .D0(D0), .D1(D1), .D2(D2), .D3(D3), .D4(D4), .D5(D5), .D6(D6), .D7(D7),
    .F(n7_1_f));
  LED led_1 (.in(n7_1_f));

  // Notes on the sheet:
  //   A0
  //   A1
  //   A2
  //   D0
  //   D1
  //   D2
  //   D3
  //   D4
  //   D5
  //   D6
  //   D7
endmodule

module shiyan2 (
  input  A,
  input  B,
  input  A_2,
  input  A_3,
  input  B_2,
  input  B_3,
  input  A0,
  input  A1,
  input  A2,
  input  A3,
  input  A_4,
  input  A_5,
  input  B_4,
  input  B_5,
  input  A_6,
  input  B_6,
  input  A_7,
  input  A_8,
  input  B_7,
  input  B_8,
  input  A_9,
  input  A_10,
  input  B_9,
  input  B_10
);

  wire n9_1_y1, n9_1_y2, n74ls00_1_out_9, n74ls00_1_out_11, n74ls00_2_out_9, n74ls00_3_out_9,
       n74ls00_4_out_9, n74ls00_4_out_11, n74ls00_4_out_12, n74ls00_5_out_9, n74ls00_5_out_11,
       n74ls00_6_out_9, n74ls00_6_out_11, n74ls00_6_out_12, n74ls00_7_out_9, n74ls00_7_out_10,
       n74ls00_7_out_11, n74ls00_7_out_12, n74ls00_8_out_9, n74ls00_8_out_11, n74ls00_8_out_12,
       n74ls00_9_out_9, n74ls00_9_out_11, n74ls00_10_out_9, n74ls00_10_out_10, n74ls00_10_out_11,
       n74ls00_10_out_12, n74ls00_11_out_9, n74ls00_11_out_11, n74ls00_11_out_12, n74ls00_12_out_9,
       n74ls00_12_out_11, not_1_out, not_2_out, not_3_out;

  LED led_1 (.in(n74ls00_4_out_12));
  not not_1 (not_1_out, n74ls00_3_out_9);
  LED led_2 (.in(not_1_out));
  _74LS00 u_74ls00_1 (
    .in_1(A_9), .in_3(A_9), .out_9(n74ls00_1_out_9), .in_5(B_9), .in_7(B_9), .out_11(n74ls00_1_out_11),
    .in_4(n74ls00_1_out_9));  // open: in_2, out_10, in_6, in_8, out_12
  LED led_3 (.in(n74ls00_2_out_9));
  LED led_4 (.in(n9_1_y1));
  _9 u_9_1 (.A0(A0), .A1(A1), .A2(A2), .A3(A3), .Y1(n9_1_y1), .Y2(n9_1_y2));
  LED led_5 (.in(n9_1_y2));
  not not_2 (not_2_out, A_6);
  not not_3 (not_3_out, B_6);
  _74LS00 u_74ls00_2 (
    .in_1(A), .in_3(B), .out_9(n74ls00_2_out_9));  // open: in_5, in_7, out_11, in_2, in_4, out_10, in_6, in_8, out_12
  _74LS00 u_74ls00_3 (
    .in_1(not_2_out), .in_3(not_3_out), .out_9(n74ls00_3_out_9));  // open: in_5, in_7, out_11, in_2, in_4, out_10, in_6, in_8, out_12
  _74LS00 u_74ls00_4 (
    .in_1(A_9), .in_3(n74ls00_1_out_11), .out_9(n74ls00_4_out_9), .in_5(n74ls00_1_out_9), .in_7(B_9),
    .out_11(n74ls00_4_out_11), .in_6(n74ls00_4_out_9), .in_8(n74ls00_4_out_11), .out_12(n74ls00_4_out_12));  // open: in_2, in_4, out_10
  LED led_6 (.in(n74ls00_6_out_12));
  _74LS00 u_74ls00_5 (
    .in_1(A_10), .in_3(A_10), .out_9(n74ls00_5_out_9), .in_5(B_10), .in_7(B_10), .out_11(n74ls00_5_out_11),
    .in_4(n74ls00_5_out_9));  // open: in_2, out_10, in_6, in_8, out_12
  _74LS00 u_74ls00_6 (
    .in_1(A_10), .in_3(n74ls00_5_out_11), .out_9(n74ls00_6_out_9), .in_5(n74ls00_5_out_9), .in_7(B_10),
    .out_11(n74ls00_6_out_11), .in_6(n74ls00_6_out_9), .in_8(n74ls00_6_out_11), .out_12(n74ls00_6_out_12));  // open: in_2, in_4, out_10
  LED led_7 (.in(n74ls00_7_out_12));
  LED led_8 (.in(n74ls00_8_out_12));
  LED led_9 (.in(n74ls00_9_out_11));
  _74LS00 u_74ls00_7 (
    .in_1(A_2), .in_3(A_2), .out_9(n74ls00_7_out_9), .in_5(B_2), .in_7(B_2), .out_11(n74ls00_7_out_11),
    .in_2(n74ls00_7_out_9), .in_4(n74ls00_7_out_11), .out_10(n74ls00_7_out_10), .in_6(n74ls00_7_out_10),
    .in_8(n74ls00_7_out_10), .out_12(n74ls00_7_out_12));
  _74LS00 u_74ls00_8 (
    .in_1(A_4), .in_3(A_4), .out_9(n74ls00_8_out_9), .in_5(B_4), .in_7(B_4), .out_11(n74ls00_8_out_11),
    .in_6(n74ls00_8_out_9), .in_8(n74ls00_8_out_11), .out_12(n74ls00_8_out_12));  // open: in_2, in_4, out_10
  _74LS00 u_74ls00_9 (
    .in_1(A_7), .in_3(B_7), .out_9(n74ls00_9_out_9), .in_5(n74ls00_9_out_9), .in_7(n74ls00_9_out_9),
    .out_11(n74ls00_9_out_11));  // open: in_2, in_4, out_10, in_6, in_8, out_12
  LED led_10 (.in(n74ls00_10_out_12));
  LED led_11 (.in(n74ls00_11_out_12));
  LED led_12 (.in(n74ls00_12_out_11));
  _74LS00 u_74ls00_10 (
    .in_1(A_3), .in_3(A_3), .out_9(n74ls00_10_out_9), .in_5(B_3), .in_7(B_3), .out_11(n74ls00_10_out_11),
    .in_2(n74ls00_10_out_9), .in_4(n74ls00_10_out_11), .out_10(n74ls00_10_out_10), .in_6(n74ls00_10_out_10),
    .in_8(n74ls00_10_out_10), .out_12(n74ls00_10_out_12));
  _74LS00 u_74ls00_11 (
    .in_1(A_5), .in_3(A_5), .out_9(n74ls00_11_out_9), .in_5(B_5), .in_7(B_5), .out_11(n74ls00_11_out_11),
    .in_6(n74ls00_11_out_9), .in_8(n74ls00_11_out_11), .out_12(n74ls00_11_out_12));  // open: in_2, in_4, out_10
  _74LS00 u_74ls00_12 (
    .in_1(A_8), .in_3(B_8), .out_9(n74ls00_12_out_9), .in_5(n74ls00_12_out_9), .in_7(n74ls00_12_out_9),
    .out_11(n74ls00_12_out_11));  // open: in_2, in_4, out_10, in_6, in_8, out_12

  // Notes on the sheet:
  //   B
  //   与非门
  //   与门
  //   或门
  //   或门
  //   异或门
  //   与非门
  //   或非门
  //   Y0
  //   Y1
  //   异或门
  //   或门
  //   或非门
  //   或门
  //   与门
  //   或非门
  //   或门
  //   与门
endmodule

module _2 (
  input  A,
  input  B,
  input  C,
  input  D,
  input  A_2,
  input  B_2,
  input  C_2,
  input  D_2,
  input  A_3,
  output F
);

  wire n74ls00_2_out_9, n74ls00_2_out_10, n74ls00_2_out_11, n74ls00_2_out_12, n74ls10_1_out_10,
       n74ls10_1_out_11, nand_1_out, nand_2_out, nand_3_out, nand_4_out, nand_5_out, undriven;

  LED led_1 (.in(n74ls10_1_out_11));
  _74LS00 u_74ls00_1 (.in_2(A_3));  // open: in_1, in_3, out_9, in_5, in_7, out_11, in_4, out_10, in_6, in_8, out_12
  nand nand_1 (nand_1_out, B, B);
  nand nand_2 (nand_2_out, D, D);
  nand nand_3 (nand_3_out, C, D);
  nand nand_4 (nand_4_out, B, D);
  nand nand_5 (nand_5_out, A, nand_1_out, nand_2_out);
  _74LS00 u_74ls00_2 (
    .in_1(D_2), .in_3(B_2), .out_9(n74ls00_2_out_9), .in_5(B_2), .in_7(B_2), .out_11(n74ls00_2_out_11),
    .in_2(C_2), .in_4(D_2), .out_10(n74ls00_2_out_10), .in_6(D_2), .in_8(D_2), .out_12(n74ls00_2_out_12));
  nand nand_6 (F, nand_3_out, nand_4_out, nand_5_out);
  _74LS10 u_74ls10_1 (
    .in_1(A_2), .in_2(n74ls00_2_out_11), .in_4(n74ls10_1_out_10), .in_6(n74ls00_2_out_10),
    .in_8(n74ls00_2_out_9), .out_11(n74ls10_1_out_11), .in_3(n74ls00_2_out_12), .out_10(n74ls10_1_out_10));  // open: in_5, in_7, in_9, out_12
  _7 u_7_1 (.A0(undriven));  // open: A1, A2, D0, D1, D2, D3, D4, D5, D6, D7, F
endmodule

module _3 (
  input  A,
  input  B,
  input  C,
  input  D,
  input  A_2,
  input  B_2,
  input  C_2,
  input  D_2,
  output F
);

  wire n74ls00_1_out_10, n74ls00_1_out_11, n74ls00_1_out_12, n74ls00_2_out_9, n74ls00_2_out_11,
       n74ls10_1_out_10, n74ls10_1_out_12, nand_1_out, nand_2_out, nand_3_out, nand_4_out, nand_5_out,
       nand_6_out;

  nand nand_1 (nand_1_out, C, C);
  nand nand_2 (nand_2_out, D, D);
  nand nand_3 (nand_3_out, B, B);
  nand nand_4 (nand_4_out, nand_1_out, D);
  nand nand_5 (nand_5_out, C, nand_2_out);
  nand nand_6 (nand_6_out, A, nand_3_out, C);
  nand nand_7 (F, nand_4_out, nand_5_out, nand_6_out);
  LED led_1 (.in(n74ls10_1_out_12));
  _74LS00 u_74ls00_1 (
    .in_5(C_2), .in_7(C_2), .out_11(n74ls00_1_out_11), .in_2(B_2), .in_4(B_2), .out_10(n74ls00_1_out_10),
    .in_6(D_2), .in_8(D_2), .out_12(n74ls00_1_out_12));  // open: in_1, in_3, out_9
  _74LS00 u_74ls00_2 (
    .in_1(n74ls00_1_out_12), .in_3(C_2), .out_9(n74ls00_2_out_9), .in_5(n74ls00_1_out_11), .in_7(D_2),
    .out_11(n74ls00_2_out_11));  // open: in_2, in_4, out_10, in_6, in_8, out_12
  _74LS10 u_74ls10_1 (
    .in_1(A_2), .in_2(C_2), .in_3(n74ls00_1_out_10), .out_10(n74ls10_1_out_10), .in_5(n74ls00_2_out_9),
    .in_7(n74ls00_2_out_11), .in_9(n74ls10_1_out_10), .out_12(n74ls10_1_out_12));  // open: in_4, in_6, in_8, out_11
endmodule

module _4 (
  input  A,
  input  B,
  input  C
);

  shiyan2 shiyan2_1 ();  // open: A, B, A_2, A_3, B_2, B_3, A0, A1, A2, A3, A_4, A_5, B_4, B_5, A_6, B_6, A_7, A_8, B_7, B_8, A_9, A_10, B_9, B_10
  LED _0 ();  // open: in
  LED _1 ();  // open: in
  LED _2 ();  // open: in
  LED _3 ();  // open: in
  LED _4 ();  // open: in
  LED _5 ();  // open: in
  LED _6 ();  // open: in
  LED _7 ();  // open: in
endmodule

module _5 (
  input  A,
  input  B,
  input  C,
  input  A_2,
  input  B_2,
  input  C_2,
  output F3,
  output F1,
  output F2,
  output F4,
  output F5,
  output F6,
  output F7,
  output F0
);

  wire n74ls00_1_out_9, n74ls00_1_out_10, n74ls00_1_out_11, n74ls00_2_out_9, n74ls00_3_out_9,
       n74ls10_1_out_10, n74ls10_1_out_11, nand_1_out, nand_2_out, nand_3_out, nand_4_out, nand_5_out,
       nand_6_out, nand_7_out, nand_8_out, nand_9_out, nand_10_out, nand_11_out, nand_12_out, nand_13_out,
       nand_14_out, nand_15_out, nand_17_out, nand_18_out, nand_19_out, undriven, undriven_2, undriven_3,
       undriven_4;

  nand nand_1 (nand_1_out, B, B);
  nand nand_2 (nand_2_out, C, C);
  nand nand_3 (nand_3_out, B, B);
  nand nand_4 (nand_4_out, C, C);
  nand nand_5 (nand_5_out, B, B);
  nand nand_6 (nand_6_out, C, C);
  nand nand_7 (nand_7_out, A, B, C);
  nand nand_8 (nand_8_out, B, B);
  nand nand_9 (nand_9_out, C, C);
  nand nand_10 (nand_10_out, undriven, nand_1_out, C);
  nand nand_11 (nand_11_out, undriven_2, B, nand_2_out);
  nand nand_12 (nand_12_out, undriven_3, B, C);
  nand nand_13 (nand_13_out, A, nand_3_out, nand_4_out);
  nand nand_14 (nand_14_out, A, nand_5_out, C);
  nand nand_15 (nand_15_out, A, B, nand_6_out);
  nand nand_16 (F7, nand_7_out, nand_7_out);
  nand nand_17 (nand_17_out, undriven_4, nand_8_out, nand_9_out);
  nand nand_18 (nand_18_out, nand_10_out, nand_10_out);
  nand nand_19 (nand_19_out, nand_11_out, nand_11_out);
  nand nand_20 (F3, nand_12_out, nand_12_out);
  nand nand_21 (F4, nand_13_out, nand_13_out);
  nand nand_22 (F5, nand_14_out, nand_14_out);
  nand nand_23 (F6, nand_15_out, nand_15_out);
  nand nand_24 (F0, nand_17_out, nand_17_out);
  _74LS00 u_74ls00_1 (
    .in_1(A_2), .in_3(A_2), .out_9(n74ls00_1_out_9), .in_5(A_2), .in_7(A_2), .out_11(n74ls00_1_out_11),
    .in_2(A_2), .in_4(A_2), .out_10(n74ls00_1_out_10), .in_6(A_2), .in_8(A_2));  // open: out_12
  _74LS00 u_74ls00_2 (
    .in_1(B_2), .in_3(B_2), .out_9(n74ls00_2_out_9), .in_5(B_2), .in_7(B_2), .in_2(B_2), .in_4(B_2),
    .in_6(B_2), .in_8(B_2));  // open: out_11, out_10, out_12
  _74LS00 u_74ls00_3 (
    .in_1(C_2), .in_3(C_2), .out_9(n74ls00_3_out_9), .in_5(C_2), .in_7(C_2), .in_2(C_2), .in_4(C_2),
    .in_6(C_2), .in_8(C_2));  // open: out_11, out_10, out_12
  _74LS10 u_74ls10_1 (
    .in_1(n74ls00_1_out_9), .in_2(n74ls00_2_out_9), .in_4(n74ls00_1_out_11), .in_6(n74ls00_3_out_9),
    .in_8(B_2), .out_11(n74ls10_1_out_11), .in_3(C_2), .out_10(n74ls10_1_out_10), .in_9(n74ls00_1_out_10));  // open: in_5, in_7, out_12
  _74LS00 u_74ls00_4 (
    .in_1(n74ls10_1_out_10), .in_3(n74ls10_1_out_10), .out_9(F1), .in_5(n74ls10_1_out_11),
    .in_7(n74ls10_1_out_11), .out_11(F2));  // open: in_2, in_4, out_10, in_6, in_8, out_12
endmodule

module _6 (
  input  A,
  input  B,
  input  C,
  output F0,
  output F1,
  output F2,
  output F3,
  output F4,
  output F5,
  output F6,
  output F7
);

  wire nand_1_out, nand_2_out, nand_3_out, nand_4_out, nand_5_out, nand_6_out, nand_7_out, nand_8_out,
       nand_9_out, nand_10_out, nand_11_out, nand_12_out, nand_13_out, nand_14_out, nand_15_out, nand_16_out,
       nand_17_out, nand_18_out, nand_19_out, nand_20_out;

  nand nand_1 (nand_1_out, A, A);
  nand nand_2 (nand_2_out, B, B);
  nand nand_3 (nand_3_out, C, C);
  nand nand_4 (nand_4_out, A, A);
  nand nand_5 (nand_5_out, B, B);
  nand nand_6 (nand_6_out, A, A);
  nand nand_7 (nand_7_out, C, C);
  nand nand_8 (nand_8_out, A, A);
  nand nand_9 (nand_9_out, B, B);
  nand nand_10 (nand_10_out, C, C);
  nand nand_11 (nand_11_out, B, B);
  nand nand_12 (nand_12_out, C, C);
  nand nand_13 (nand_13_out, A, B, C);
  nand nand_14 (nand_14_out, nand_1_out, nand_2_out, nand_3_out);
  nand nand_15 (nand_15_out, nand_4_out, nand_5_out, C);
  nand nand_16 (nand_16_out, nand_6_out, B, nand_7_out);
  nand nand_17 (nand_17_out, nand_8_out, B, C);
  nand nand_18 (nand_18_out, A, nand_9_out, nand_10_out);
  nand nand_19 (nand_19_out, A, nand_11_out, C);
  nand nand_20 (nand_20_out, A, B, nand_12_out);
  nand nand_21 (F7, nand_13_out, nand_13_out);
  nand nand_22 (F0, nand_14_out, nand_14_out);
  nand nand_23 (F1, nand_15_out, nand_15_out);
  nand nand_24 (F2, nand_16_out, nand_16_out);
  nand nand_25 (F3, nand_17_out, nand_17_out);
  nand nand_26 (F4, nand_18_out, nand_18_out);
  nand nand_27 (F5, nand_19_out, nand_19_out);
  nand nand_28 (F6, nand_20_out, nand_20_out);
endmodule

module _7 (
  input  A0,
  input  A1,
  input  A2,
  input  D0,
  input  D1,
  input  D2,
  input  D3,
  input  D4,
  input  D5,
  input  D6,
  input  D7,
  output F
);

  wire and_1_out, and_2_out, and_3_out, and_4_out, and_5_out, and_6_out, and_7_out, and_8_out, not_1_out,
       not_2_out, not_3_out, not_4_out, not_5_out, not_6_out, not_7_out, not_8_out, not_9_out, not_10_out,
       not_11_out, not_12_out;

  not not_1 (not_1_out, A1);
  not not_2 (not_2_out, A2);
  not not_3 (not_3_out, A0);
  not not_4 (not_4_out, A1);
  not not_5 (not_5_out, A2);
  not not_6 (not_6_out, A2);
  not not_7 (not_7_out, A0);
  not not_8 (not_8_out, A2);
  not not_9 (not_9_out, A1);
  not not_10 (not_10_out, A0);
  not not_11 (not_11_out, A1);
  not not_12 (not_12_out, A0);
  and and_1 (and_1_out, not_1_out, not_2_out, not_3_out, D0);
  and and_2 (and_2_out, not_4_out, not_5_out, A0, D1);
  and and_3 (and_3_out, A1, not_6_out, not_7_out, D2);
  and and_4 (and_4_out, A1, not_8_out, A0, D3);
  and and_5 (and_5_out, not_9_out, A2, not_10_out, D4);
  and and_6 (and_6_out, not_11_out, A2, A0, D5);
  and and_7 (and_7_out, A1, A2, not_12_out, D6);
  and and_8 (and_8_out, A1, A2, A0, D7);
  or or_1 (F, and_1_out, and_2_out, and_3_out, and_4_out, and_5_out, and_6_out, and_7_out, and_8_out);
endmodule

module _8 (
  input  A,
  input  B,
  input  C
);

  wire n74ls00_1_out_9, n74ls00_1_out_11, n74ls00_1_out_12, n74ls00_2_out_9, n74ls00_2_out_10,
       n74ls00_2_out_11, n74ls00_2_out_12, n74ls00_3_out_9, n74ls00_3_out_10, n74ls00_3_out_11,
       n74ls00_3_out_12, n74ls10_1_out_10, n74ls10_1_out_11, n74ls10_1_out_12, n74ls10_2_out_10,
       n74ls10_2_out_11, n74ls10_2_out_12, n74ls10_3_out_10, n74ls10_3_out_11;

  _74LS00 u_74ls00_1 (
    .in_1(A), .in_3(A), .out_9(n74ls00_1_out_9), .in_5(B), .in_7(B), .out_11(n74ls00_1_out_11), .in_6(C),
    .in_8(C), .out_12(n74ls00_1_out_12));  // open: in_2, in_4, out_10
  _74LS10 u_74ls10_1 (
    .in_1(n74ls00_1_out_9), .in_2(n74ls00_1_out_11), .in_4(n74ls00_1_out_9), .in_6(n74ls00_1_out_11),
    .in_8(C), .out_11(n74ls10_1_out_11), .in_3(n74ls00_1_out_12), .out_10(n74ls10_1_out_10),
    .in_5(n74ls00_1_out_9), .in_7(n74ls00_1_out_12), .in_9(B), .out_12(n74ls10_1_out_12));
  _74LS10 u_74ls10_2 (
    .in_1(n74ls00_1_out_9), .in_2(C), .in_4(A), .in_6(n74ls00_1_out_11), .in_8(n74ls00_1_out_12),
    .out_11(n74ls10_2_out_11), .in_3(B), .out_10(n74ls10_2_out_10), .in_5(A), .in_7(n74ls00_1_out_11),
    .in_9(C), .out_12(n74ls10_2_out_12));
  _74LS10 u_74ls10_3 (
    .in_1(A), .in_2(B), .in_4(A), .in_6(B), .in_8(C), .out_11(n74ls10_3_out_11), .in_3(n74ls00_1_out_12),
    .out_10(n74ls10_3_out_10));  // open: in_5, in_7, in_9, out_12
  _74LS00 u_74ls00_2 (
    .in_1(n74ls10_1_out_10), .in_3(n74ls10_1_out_10), .out_9(n74ls00_2_out_9), .in_5(n74ls10_1_out_12),
    .in_7(n74ls10_1_out_12), .out_11(n74ls00_2_out_11), .in_2(n74ls10_1_out_11), .in_4(n74ls10_1_out_11),
    .out_10(n74ls00_2_out_10), .in_6(n74ls10_2_out_10), .in_8(n74ls10_2_out_10), .out_12(n74ls00_2_out_12));
  _74LS00 u_74ls00_3 (
    .in_1(n74ls10_2_out_11), .in_3(n74ls10_2_out_11), .out_9(n74ls00_3_out_9), .in_5(n74ls10_2_out_12),
    .in_7(n74ls10_2_out_12), .out_11(n74ls00_3_out_11), .in_2(n74ls10_3_out_10), .in_4(n74ls10_3_out_10),
    .out_10(n74ls00_3_out_10), .in_6(n74ls10_3_out_11), .in_8(n74ls10_3_out_11), .out_12(n74ls00_3_out_12));
  LED _0 (.in(n74ls00_2_out_9));
  LED _1 (.in(n74ls00_2_out_10));
  LED _2 (.in(n74ls00_2_out_11));
  LED _3 (.in(n74ls00_2_out_12));
  LED _4 (.in(n74ls00_3_out_9));
  LED _5 (.in(n74ls00_3_out_11));
  LED _6 (.in(n74ls00_3_out_10));
  LED _7 (.in(n74ls00_3_out_12));
endmodule

module _9 (
  input  A0,
  input  A1,
  input  A2,
  input  A3,
  output Y1,
  output Y2
);

  wire not_1_out;

  or or_1 (Y1, A1, A0);
  not not_1 (not_1_out, A1);
  or or_2 (Y2, not_1_out, A0);
endmodule

module _3main (
  input  A0,
  input  A1,
  input  cc,
  input  B,
  input  A,
  input  A_2,
  input  B_2,
  input  A0_2,
  input  C,
  input  A1_2,
  input  A2,
  input  A3,
  input  B0,
  input  B1,
  input  B2,
  input  B3,
  input  D,
  input  J,
  input  Clk,
  input  K,
  input  Clk_2,
  output A0_3,
  output A1_3,
  output Q,
  output nQ,
  output Q_2
);

  wire and_1_out, and_2_out, n4_2_1_y0, n4_2_1_y1, n4_2_1_y2, n4_2_1_y3, n237_1_f, not_1_out, not_2_out,
       or_1_out, \全加器_2_c , \全加器_2_s , \全加器_3_c , \全加器_3_s , \全加器_4_c , \全加器_4_s , \全加器_5_c , \全加器_5_s ;

  LED Y3 (.in(n4_2_1_y3));
  LED Y0 (.in(n4_2_1_y0));
  _4_2 u_4_2_1 (.A0(A0), .A1(A1), .Y0(n4_2_1_y0), .Y1(n4_2_1_y1), .Y2(n4_2_1_y2), .Y3(n4_2_1_y3));
  LED Y1 (.in(n4_2_1_y1));
  LED Y2 (.in(n4_2_1_y2));
  LED F (.in(n237_1_f));
  _237 u_237_1 (.A(A_2), .B(B_2), .C(C), .F(n237_1_f));
  D d_1 (.D(D), .Clk(Clk), .Q(Q), .nQ(nQ));
  JK jk_1 ();  // open: J, K, Clk, Q
  \全加器  \u_全加器_1  (.cc(cc), .B(B), .A(A), .S(A0_3), .C(A1_3));
  \全加器  \u_全加器_2  (.cc(1'b0), .B(B0), .A(A0_2), .S(\全加器_2_s ), .C(\全加器_2_c ));
  LED Y0_2 (.in(\全加器_2_s ));
  LED Y1_2 (.in(\全加器_3_s ));
  \全加器  \u_全加器_3  (.cc(\全加器_2_c ), .B(B1), .A(A1_2), .S(\全加器_3_s ), .C(\全加器_3_c ));
  LED Y2_2 (.in(\全加器_4_s ));
  \全加器  \u_全加器_4  (.cc(\全加器_3_c ), .B(B2), .A(A2), .S(\全加器_4_s ), .C(\全加器_4_c ));
  LED Y3_2 (.in(\全加器_5_s ));
  \全加器  \u_全加器_5  (.cc(\全加器_4_c ), .B(B3), .A(A3), .S(\全加器_5_s ), .C(\全加器_5_c ));
  LED Y4 (.in(\全加器_5_c ));
  not not_1 (not_1_out, Q_2);
  not not_2 (not_2_out, K);
  and and_1 (and_1_out, J, not_1_out);
  and and_2 (and_2_out, not_2_out, Q_2);
  or or_1 (or_1_out, and_1_out, and_2_out);
  D d_2 (.D(or_1_out), .Clk(Clk_2), .Q(Q_2));  // open: nQ

  // Notes on the sheet:
  //   D
  //   Clk
  //   2：4译码器
  //   全加器
  //   Clk
endmodule

module _4_2 (
  input  A0,
  input  A1,
  output Y0,
  output Y1,
  output Y2,
  output Y3
);

  wire n74ls138_1_out_7, n74ls138_1_out_8, n74ls138_1_out_9, n74ls138_1_out_10;

  _74LS138 u_74ls138_1 (
    .in_1(A0), .in_2(A1), .in_3(1'b0), .in_4(1'b0), .in_5(1'b0), .in_6(1'b1), .out_7(n74ls138_1_out_7),
    .out_8(n74ls138_1_out_8), .out_9(n74ls138_1_out_9), .out_10(n74ls138_1_out_10));  // open: out_13, out_11, out_12, out_14
  not not_1 (Y0, n74ls138_1_out_7);
  not not_2 (Y1, n74ls138_1_out_8);
  not not_3 (Y2, n74ls138_1_out_9);
  not not_4 (Y3, n74ls138_1_out_10);
endmodule

module _237 (
  input  A,
  input  B,
  input  C,
  output F
);

  wire n74ls138_1_out_9, n74ls138_1_out_12, n74ls138_1_out_13;

  _74LS138 u_74ls138_1 (
    .in_1(A), .in_2(B), .in_3(C), .in_4(1'b0), .in_5(1'b0), .in_6(1'b1), .out_13(n74ls138_1_out_13),
    .out_9(n74ls138_1_out_9), .out_12(n74ls138_1_out_12));  // open: out_7, out_8, out_10, out_11, out_14
  nand nand_1 (F, n74ls138_1_out_9, n74ls138_1_out_12, n74ls138_1_out_13);
endmodule

module \全加器  (
  input  cc,
  input  B,
  input  A,
  output S,
  output C
);

  wire n74ls138_1_out_8, n74ls138_1_out_9, n74ls138_1_out_10, n74ls138_1_out_11, n74ls138_1_out_12,
       n74ls138_1_out_13, n74ls138_1_out_14;

  _74LS138 u_74ls138_1 (
    .in_1(cc), .in_2(B), .in_3(A), .in_4(1'b0), .in_5(1'b0), .in_6(1'b1), .out_13(n74ls138_1_out_13),
    .out_8(n74ls138_1_out_8), .out_9(n74ls138_1_out_9), .out_10(n74ls138_1_out_10),
    .out_11(n74ls138_1_out_11), .out_12(n74ls138_1_out_12), .out_14(n74ls138_1_out_14));  // open: out_7
  nand nand_1 (S, n74ls138_1_out_9, n74ls138_1_out_8, n74ls138_1_out_11, n74ls138_1_out_13);
  nand nand_2 (C, n74ls138_1_out_10, n74ls138_1_out_12, n74ls138_1_out_14, n74ls138_1_out_13);
endmodule

module x (
);

  \全加器  \u_全加器_1  ();  // open: cc, B, A, S, C
endmodule

module D (
  input  D,
  input  Clk,
  output Q,
  output nQ
);

  wire nand_1_out, nand_2_out;

  nand nand_1 (nand_1_out, D, Clk);
  nand nand_2 (nand_2_out, Clk, nand_1_out);
  nand nand_3 (Q, nand_1_out, nQ);
  nand nand_4 (nQ, Q, nand_2_out);
endmodule

module JK (
  input  J,
  input  K,
  input  Clk,
  output Q
);

  wire and_1_out, and_2_out, not_1_out, not_2_out, or_1_out;

  not not_1 (not_1_out, Q);
  not not_2 (not_2_out, K);
  and and_1 (and_1_out, J, not_1_out);
  and and_2 (and_2_out, not_2_out, Q);
  or or_1 (or_1_out, and_1_out, and_2_out);
  D d_1 (.D(or_1_out), .Clk(Clk), .Q(Q));  // open: nQ

  // Notes on the sheet:
  //   Clk
endmodule
