// Logisim project 数字逻辑实验三.circ as structural Verilog: 21 circuits, main circuit 74LS00
module _74LS00 (
  input  in_1,
  input  in_2,
  input  in_3,
  input  in_4,
  input  in_5,
  input  in_6,
  input  in_7,
  input  in_8,
  output out_9,
  output out_10,
  output out_11,
  output out_12
);

  nand nand_1 (out_9, in_3, in_1);
  nand nand_2 (out_11, in_7, in_5);
  nand nand_3 (out_10, in_2, in_4);
  nand nand_4 (out_12, in_6, in_8);
endmodule

module _74LS08 (
  input  in_1,
  input  in_2,
  input  in_3,
  input  in_4,
  input  in_5,
  input  in_6,
  input  in_7,
  input  in_8,
  output out_9,
  output out_10,
  output out_11,
  output out_12
);

  and and_1 (out_9, in_3, in_1);
  and and_2 (out_11, in_7, in_5);
  and and_3 (out_10, in_2, in_4);
  and and_4 (out_12, in_6, in_8);
endmodule

module _74LS04 (
  input  in_1,
  input  in_2,
  input  in_3,
  input  in_4,
  input  in_5,
  input  in_6,
  output out_7,
  output out_8,
  output out_9,
  output out_10,
  output out_11,
  output out_12
);

  not not_1 (out_7, in_1);
  not not_2 (out_9, in_3);
  not not_3 (out_11, in_5);
  not not_4 (out_8, in_2);
  not not_5 (out_10, in_4);
  not not_6 (out_12, in_6);
endmodule

module _74LS10 (
  input  in_1,
  input  in_2,
  input  in_3,
  input  in_4,
  input  in_5,
  input  in_6,
  input  in_7,
  input  in_8,
  input  in_9,
  output out_10,
  output out_11,
  output out_12
);

  nand nand_1 (out_11, in_8, in_6, in_4);
  nand nand_2 (out_10, in_2, in_1, in_3);
  nand nand_3 (out_12, in_5, in_7, in_9);
endmodule

module _74LS20 (
  input  in_1,
  input  in_2,
  input  in_3,
  input  in_4,
  input  in_5,
  input  in_6,
  input  in_7,
  input  in_8,
  input  in_9,
  input  in_10,
  output out_11,
  output out_12
);

  nand nand_1 (out_11, in_9, in_7, in_3, in_1);
  nand nand_2 (out_12, in_2, in_4, in_8, in_10);
endmodule

module _74LS32 (
  input  in_1,
  input  in_2,
  input  in_3,
  input  in_4,
  input  in_5,
  input  in_6,
  input  in_7,
  input  in_8,
  output out_9,
  output out_10,
  output out_11,
  output out_12
);

  or or_1 (out_9, in_3, in_1);
  or or_2 (out_11, in_7, in_5);
  or or_3 (out_10, in_2, in_4);
  or or_4 (out_12, in_6, in_8);
endmodule

module _74LS86 (
  input  in_1,
  input  in_2,
  input  in_3,
  input  in_4,
  input  in_5,
  input  in_6,
  input  in_7,
  input  in_8,
  output out_9,
  output out_10,
  output out_11,
  output out_12
);

  xor xor_1 (out_9, in_3, in_1);
  xor xor_2 (out_11, in_7, in_5);
  xor xor_3 (out_10, in_2, in_4);
  xor xor_4 (out_12, in_6, in_8);
endmodule

module _74LS138 (
  input  in_1,
  input  in_2,
  input  in_3,
  input  in_4,
  input  in_5,
  input  in_6,
  output out_7,
  output out_8,
  output out_9,
  output out_10,
  output out_11,
  output out_12,
  output out_13,
  output out_14
);

  wire and_1_out, decoder_1_out0, decoder_1_out1, decoder_1_out2, decoder_1_out3, decoder_1_out4,
       decoder_1_out5, decoder_1_out6, decoder_1_out7;

  and and_1 (and_1_out, ~in_4, ~in_5, in_6);  // AND_Gate
  not not_1 (out_13, decoder_1_out7);
  Decoder #(.select(3), .disabled(0)) decoder_1 (
    .out0(decoder_1_out0), .out1(decoder_1_out1), .out2(decoder_1_out2), .out3(decoder_1_out3),
    .out4(decoder_1_out4), .out5(decoder_1_out5), .out6(decoder_1_out6), .out7(decoder_1_out7),
    .sel({in_3, in_2, in_1}), .en(and_1_out));
  not not_2 (out_7, decoder_1_out0);
  not not_3 (out_8, decoder_1_out1);
  not not_4 (out_9, decoder_1_out2);
  not not_5 (out_10, decoder_1_out3);
  not not_6 (out_11, decoder_1_out4);
  not not_7 (out_12, decoder_1_out5);
  not not_8 (out_14, decoder_1_out6);
endmodule

module _3main (
  input  in_1,
  input  in_2,
  input  in_3,
  input  in_4,
  input  in_5,
  input  in_6,
  input  A0,
  input  A1,
  input  cc,
  input  B,
  input  A,
  input  A_2,
  input  B_2,
  input  A0_2,
  input  C,
  input  A1_2,
  input  A2,
  input  A3,
  input  B0,
  input  B1,
  input  B2,
  input  B3,
  input  D,
  input  Clk,
  input  J,
  input  K,
  input  Clk_2,
  output out_28,
  output out_29,
  output out_30,
  output out_31,
  output out_32,
  output out_33,
  output out_34,
  output out_35,
  output A0_3,
  output A1_3,
  output Q,
  output nQ,
  output Q_2
);

  wire n4_2_1_y0, n4_2_1_y1, n4_2_1_y2, n4_2_1_y3, n237_1_f, \全加器_2_c , \全加器_2_s , \全加器_3_c , \全加器_3_s ,
       \全加器_4_c , \全加器_4_s , \全加器_5_c , \全加器_5_s ;

  LED Y3 (.in(n4_2_1_y3));
  LED Y0 (.in(n4_2_1_y0));
  _4_2 u_4_2_1 (.A0(A0), .A1(A1), .Y0(n4_2_1_y0), .Y1(n4_2_1_y1), .Y2(n4_2_1_y2), .Y3(n4_2_1_y3));
  LED Y1 (.in(n4_2_1_y1));
  LED Y2 (.in(n4_2_1_y2));
  LED F (.in(n237_1_f));
  _237 u_237_1 (.A(A_2), .B(B_2), .C(C), .F(n237_1_f));
  D d_1 (.D(D), .Clk(Clk), .Q(Q), .nQ(nQ));
  _74LS138 u_74ls138_1 (
    .in_1(in_1), .in_2(in_2), .in_3(in_3), .in_4(in_4), .in_5(in_5), .in_6(in_6), .out_13(out_33),
    .out_7(out_28), .out_8(out_29), .out_9(out_30), .out_10(out_31), .out_11(out_32), .out_12(out_34),
    .out_14(out_35));
  \全加器  \u_全加器_1  (.cc(cc), .B(B), .A(A), .S(A0_3), .C(A1_3));
  \全加器  \u_全加器_2  (.cc(1'b0), .B(B0), .A(A0_2), .S(\全加器_2_s ), .C(\全加器_2_c ));
  LED Y0_2 (.in(\全加器_2_s ));
  \全加器  \u_全加器_3  (.cc(\全加器_2_c ), .B(B1), .A(A1_2), .S(\全加器_3_s ), .C(\全加器_3_c ));
  LED Y1_2 (.in(\全加器_3_s ));
  LED Y2_2 (.in(\全加器_4_s ));
  \全加器  \u_全加器_4  (.cc(\全加器_3_c ), .B(B2), .A(A2), .S(\全加器_4_s ), .C(\全加器_4_c ));
  LED Y3_2 (.in(\全加器_5_s ));
  \全加器  \u_全加器_5  (.cc(\全加器_4_c ), .B(B3), .A(A3), .S(\全加器_5_s ), .C(\全加器_5_c ));
  LED Y4 (.in(\全加器_5_c ));
  JK jk_1 (.J(J), .K(K), .Clk(Clk_2), .Q(Q_2));

  // Notes on the sheet:
  //   D
  //   Clk
  //   2：4译码器
  //   全加器
endmodule

module _4_2 (
  input  A0,
  input  A1,
  output Y0,
  output Y1,
  output Y2,
  output Y3
);

  wire n74ls138_1_out_7, n74ls138_1_out_8, n74ls138_1_out_9, n74ls138_1_out_10;

  _74LS138 u_74ls138_1 (
    .in_1(A0), .in_2(A1), .in_3(1'b0), .in_4(1'b0), .in_5(1'b0), .in_6(1'b1), .out_7(n74ls138_1_out_7),
    .out_8(n74ls138_1_out_8), .out_9(n74ls138_1_out_9), .out_10(n74ls138_1_out_10));  // open: out_13, out_11, out_12, out_14
  not not_1 (Y0, n74ls138_1_out_7);
  not not_2 (Y1, n74ls138_1_out_8);
  not not_3 (Y2, n74ls138_1_out_9);
  not not_4 (Y3, n74ls138_1_out_10);
endmodule

module _237 (
  input  A,
  input  B,
  input  C,
  output F
);

  wire n74ls138_1_out_9, n74ls138_1_out_12, n74ls138_1_out_13;

  _74LS138 u_74ls138_1 (
    .in_1(A), .in_2(B), .in_3(C), .in_4(1'b0), .in_5(1'b0), .in_6(1'b1), .out_13(n74ls138_1_out_13),
    .out_9(n74ls138_1_out_9), .out_12(n74ls138_1_out_12));  // open: out_7, out_8, out_10, out_11, out_14
  nand nand_1 (F, n74ls138_1_out_9, n74ls138_1_out_12, n74ls138_1_out_13);
endmodule

module \全加器  (
  input  cc,
  input  B,
  input  A,
  output S,
  output C
);

  wire n74ls138_1_out_8, n74ls138_1_out_9, n74ls138_1_out_10, n74ls138_1_out_11, n74ls138_1_out_12,
       n74ls138_1_out_13, n74ls138_1_out_14;

  _74LS138 u_74ls138_1 (
    .in_1(cc), .in_2(B), .in_3(A), .in_4(1'b0), .in_5(1'b0), .in_6(1'b1), .out_13(n74ls138_1_out_13),
    .out_8(n74ls138_1_out_8), .out_9(n74ls138_1_out_9), .out_10(n74ls138_1_out_10),
    .out_11(n74ls138_1_out_11), .out_12(n74ls138_1_out_12), .out_14(n74ls138_1_out_14));  // open: out_7
  nand nand_1 (S, n74ls138_1_out_9, n74ls138_1_out_8, n74ls138_1_out_11, n74ls138_1_out_13);
  nand nand_2 (C, n74ls138_1_out_10, n74ls138_1_out_12, n74ls138_1_out_14, n74ls138_1_out_13);
endmodule

module x (
);

  \全加器  \u_全加器_1  ();  // open: cc, B, A, S, C
endmodule

module D (
  input  D,
  input  Clk,
  output Q,
  output nQ
);

  wire nand_1_out, nand_2_out;

  nand nand_1 (nand_1_out, D, Clk);
  nand nand_2 (nand_2_out, Clk, nand_1_out);
  nand nand_3 (Q, nand_1_out, nQ);
  nand nand_4 (nQ, Q, nand_2_out);
endmodule

module JK (
  input  J,
  input  K,
  input  Clk,
  output Q
);

  wire and_1_out, and_2_out, not_1_out, not_2_out, or_1_out;

  not not_1 (not_1_out, Q);
  not not_2 (not_2_out, K);
  and and_1 (and_1_out, J, not_1_out);
  and and_2 (and_2_out, not_2_out, Q);
  or or_1 (or_1_out, and_1_out, and_2_out);
  D d_1 (.D(or_1_out), .Clk(Clk), .Q(Q));  // open: nQ

  // Notes on the sheet:
  //   Clk
endmodule

module _74LS48 (
  input  D,
  input  C,
  input  B,
  input  A,
  output a_2,
  output b_2,
  output c_2,
  output d_2,
  output e,
  output f,
  output g
);

  wire and_1_out, and_2_out, and_3_out, and_4_out, and_5_out, and_6_out, and_7_out, and_8_out, and_9_out,
       and_10_out, and_11_out, and_12_out, and_13_out, and_14_out, and_15_out, and_16_out, and_17_out,
       and_18_out, and_19_out, and_20_out, and_21_out, and_22_out, and_23_out, and_24_out, and_25_out,
       and_26_out, and_27_out, not_1_out, not_2_out, not_3_out, not_4_out, not_5_out, not_6_out, not_7_out,
       not_8_out, not_9_out, not_10_out, not_11_out, not_12_out, not_13_out, not_14_out, not_15_out,
       not_16_out, not_17_out, not_18_out, not_19_out, not_20_out, not_21_out, not_22_out, not_23_out,
       not_24_out, not_25_out, not_26_out, not_27_out, not_28_out, not_29_out, not_30_out, not_31_out,
       not_32_out, not_33_out, not_34_out, not_35_out, not_36_out, not_37_out;

  not not_1 (not_1_out, D);
  and and_1 (and_1_out, not_1_out, not_2_out, not_3_out);
  not not_2 (not_2_out, C);
  not not_3 (not_3_out, A);
  not not_4 (not_4_out, D);
  not not_5 (not_5_out, C);
  and and_2 (and_2_out, not_4_out, not_5_out, B);
  not not_6 (not_6_out, D);
  and and_3 (and_3_out, not_6_out, C, A);
  not not_7 (not_7_out, C);
  and and_4 (and_4_out, D, not_7_out, not_8_out);
  not not_8 (not_8_out, B);
  and and_5 (and_5_out, D, not_9_out, A);
  not not_9 (not_9_out, B);
  not not_10 (not_10_out, D);
  and and_6 (and_6_out, not_10_out, not_11_out);
  not not_11 (not_11_out, C);
  not not_12 (not_12_out, C);
  and and_7 (and_7_out, not_12_out, not_13_out);
  not not_13 (not_13_out, B);
  not not_14 (not_14_out, B);
  and and_8 (and_8_out, not_14_out, not_15_out);
  not not_15 (not_15_out, A);
  and and_9 (and_9_out, C, B, A);
  not not_16 (not_16_out, C);
  and and_10 (and_10_out, not_16_out, not_17_out);
  not not_17 (not_17_out, B);
  not not_18 (not_18_out, B);
  and and_11 (and_11_out, not_18_out, not_19_out);
  not not_19 (not_19_out, A);
  and and_12 (and_12_out, B, A);
  not not_20 (not_20_out, D);
  and and_13 (and_13_out, not_20_out, C);
  not not_21 (not_21_out, C);
  and and_14 (and_14_out, not_21_out, not_22_out);
  not not_22 (not_22_out, A);
  not not_23 (not_23_out, C);
  and and_15 (and_15_out, not_23_out, B);
  and and_16 (and_16_out, B, not_24_out);
  not not_24 (not_24_out, A);
  not not_25 (not_25_out, B);
  and and_17 (and_17_out, C, not_25_out, A);
  not not_26 (not_26_out, C);
  and and_18 (and_18_out, not_26_out, not_27_out);
  not not_27 (not_27_out, A);
  and and_19 (and_19_out, B, not_28_out);
  not not_28 (not_28_out, A);
  not not_29 (not_29_out, B);
  and and_20 (and_20_out, not_29_out, not_30_out);
  not not_30 (not_30_out, A);
  and and_21 (and_21_out, C, not_31_out);
  not not_31 (not_31_out, B);
  and and_22 (and_22_out, C, not_32_out);
  not not_32 (not_32_out, A);
  and and_23 (and_23_out, D, not_33_out);
  not not_33 (not_33_out, B);
  not not_34 (not_34_out, C);
  and and_24 (and_24_out, not_34_out, B);
  and and_25 (and_25_out, C, not_35_out);
  not not_35 (not_35_out, B);
  and and_26 (and_26_out, C, not_36_out);
  not not_36 (not_36_out, A);
  and and_27 (and_27_out, D, not_37_out);
  not not_37 (not_37_out, C);
  or or_1 (a_2, and_1_out, and_2_out, and_3_out, and_4_out, and_5_out);
  or or_2 (b_2, and_6_out, and_7_out, and_8_out, and_9_out);
  or or_3 (c_2, and_10_out, and_11_out, and_12_out, and_13_out);
  or or_4 (d_2, and_14_out, and_15_out, and_16_out, and_17_out);
  or or_5 (e, and_18_out, and_19_out);
  or or_6 (f, and_20_out, and_21_out, and_22_out, and_23_out);
  or or_7 (g, and_24_out, and_25_out, and_26_out, and_27_out);
endmodule

module _1 (
  input  CLK,
  input  in_2,
  output Q2,
  output Q1,
  output Q0
);

  wire and_1_out;

  J_K_Flip_Flop j_k_ff_1 (.J(and_1_out), .clk(CLK), .K(and_1_out), .Q(Q2), .reset(in_2));  // open: Qn, preset, en
  and and_1 (and_1_out, Q0, Q1);
  J_K_Flip_Flop j_k_ff_2 (.J(Q0), .clk(CLK), .K(Q0), .Q(Q1), .reset(in_2));  // open: Qn, preset, en
  J_K_Flip_Flop j_k_ff_3 (.J(1'b1), .clk(CLK), .K(1'b1), .Q(Q0), .reset(in_2));  // open: Qn, preset, en
endmodule

module mian (
  input  _3,
  input  _2,
  input  _1,
  input  _0,
  input  in_5,
  input  CLK,
  input  in_7,
  input  [1:0] _0_2,
  input  L,
  input  R,
  input  _3_2,
  input  _2_2,
  input  _1_2,
  input  _0_3,
  input  _3_3,
  input  _3_4,
  input  _2_3,
  input  _2_4,
  input  _1_3,
  input  _1_4,
  input  _0_4,
  input  _0_5,
  input  _3_5,
  input  _3_6,
  input  _2_5,
  input  _2_6,
  input  _1_5,
  input  _1_6,
  input  _0_6,
  input  _0_7
);

  wire clock_1_out, n1_1_q0, n1_1_q1, n1_1_q2, n2_1_q0, n2_1_q1, n2_1_q2, n2_1_q3, n3_1_a_2, n3_1_b_2,
       n3_1_c_2, n3_1_d_2, n3_1_e, n3_1_f, n3_1_g, n74ls48_1_a_2, n74ls48_1_b_2, n74ls48_1_c_2,
       n74ls48_1_d_2, n74ls48_1_e, n74ls48_1_f, n74ls48_1_g, n74ls48_2_a_2, n74ls48_2_b_2, n74ls48_2_c_2,
       n74ls48_2_d_2, n74ls48_2_e, n74ls48_2_f, n74ls48_2_g, n74ls48_3_a_2, n74ls48_3_b_2, n74ls48_3_c_2,
       n74ls48_3_d_2, n74ls48_3_e, n74ls48_3_f, n74ls48_3_g, n74ls48_4_a_2, n74ls48_4_b_2, n74ls48_4_c_2,
       n74ls48_4_d_2, n74ls48_4_e, n74ls48_4_f, n74ls48_4_g, n74ls48_5_a_2, n74ls48_5_b_2, n74ls48_5_c_2,
       n74ls48_5_d_2, n74ls48_5_e, n74ls48_5_f, n74ls48_5_g, n74ls48_6_a_2, n74ls48_6_b_2, n74ls48_6_c_2,
       n74ls48_6_d_2, n74ls48_6_e, n74ls48_6_f, n74ls48_6_g;

  _3 u_3_1 (
    .D(_3), .C(_2), .B(_1), .A(_0), .a_2(n3_1_a_2), .b_2(n3_1_b_2), .c_2(n3_1_c_2), .d_2(n3_1_d_2),
    .e(n3_1_e), .f(n3_1_f), .g(n3_1_g));
  _2 u_2_1 (
    .in_1(CLK), .in_2(in_7), .S(_0_2), .Q3(n2_1_q3), .Q2(n2_1_q2), .Q1(n2_1_q1), .Q0(n2_1_q0), .DL(L),
    .DR(R), ._3(_3_2), ._2(_2_2), ._1(_1_2), ._0(_0_3));
  _74LS48 u_74ls48_1 (
    .D(_3_3), .C(_2_3), .B(_1_3), .A(_0_4), .a_2(n74ls48_1_a_2), .b_2(n74ls48_1_b_2), .c_2(n74ls48_1_c_2),
    .d_2(n74ls48_1_d_2), .e(n74ls48_1_e), .f(n74ls48_1_f), .g(n74ls48_1_g));
  _74LS48 u_74ls48_2 (
    .D(_3_5), .C(_2_5), .B(_1_5), .A(_0_6), .a_2(n74ls48_2_a_2), .b_2(n74ls48_2_b_2), .c_2(n74ls48_2_c_2),
    .d_2(n74ls48_2_d_2), .e(n74ls48_2_e), .f(n74ls48_2_f), .g(n74ls48_2_g));
  _7_Segment_Display u_7_segment_display_1 (
    .g(n3_1_g), .f(n3_1_f), .a(n3_1_a_2), .b(n3_1_b_2), .e(n3_1_e), .d(n3_1_d_2), .c(n3_1_c_2));  // open: dp
  _74LS48 u_74ls48_3 (
    .D(n2_1_q3), .C(n2_1_q2), .B(n2_1_q1), .A(n2_1_q0), .a_2(n74ls48_3_a_2), .b_2(n74ls48_3_b_2),
    .c_2(n74ls48_3_c_2), .d_2(n74ls48_3_d_2), .e(n74ls48_3_e), .f(n74ls48_3_f), .g(n74ls48_3_g));
  Clock clock_1 (.out(clock_1_out));
  _1 u_1_1 (.CLK(clock_1_out), .Q2(n1_1_q2), .Q1(n1_1_q1), .Q0(n1_1_q0), .in_2(in_5));
  _7_Segment_Display u_7_segment_display_2 (
    .g(n74ls48_1_g), .f(n74ls48_1_f), .a(n74ls48_1_a_2), .b(n74ls48_1_b_2), .e(n74ls48_1_e),
    .d(n74ls48_1_d_2), .c(n74ls48_1_c_2));  // open: dp
  _7_Segment_Display u_7_segment_display_3 (
    .g(n74ls48_2_g), .f(n74ls48_2_f), .a(n74ls48_2_a_2), .b(n74ls48_2_b_2), .e(n74ls48_2_e),
    .d(n74ls48_2_d_2), .c(n74ls48_2_c_2));  // open: dp
  _7_Segment_Display u_7_segment_display_4 (
    .g(n74ls48_3_g), .f(n74ls48_3_f), .a(n74ls48_3_a_2), .b(n74ls48_3_b_2), .e(n74ls48_3_e),
    .d(n74ls48_3_d_2), .c(n74ls48_3_c_2));  // open: dp
  _74LS48 u_74ls48_4 (
    .D(1'b0), .C(n1_1_q2), .B(n1_1_q1), .A(n1_1_q0), .a_2(n74ls48_4_a_2), .b_2(n74ls48_4_b_2),
    .c_2(n74ls48_4_c_2), .d_2(n74ls48_4_d_2), .e(n74ls48_4_e), .f(n74ls48_4_f), .g(n74ls48_4_g));
  _74LS48 u_74ls48_5 (
    .D(_3_4), .C(_2_4), .B(_1_4), .A(_0_5), .a_2(n74ls48_5_a_2), .b_2(n74ls48_5_b_2), .c_2(n74ls48_5_c_2),
    .d_2(n74ls48_5_d_2), .e(n74ls48_5_e), .f(n74ls48_5_f), .g(n74ls48_5_g));
  _74LS48 u_74ls48_6 (
    .D(_3_6), .C(_2_6), .B(_1_6), .A(_0_7), .a_2(n74ls48_6_a_2), .b_2(n74ls48_6_b_2), .c_2(n74ls48_6_c_2),
    .d_2(n74ls48_6_d_2), .e(n74ls48_6_e), .f(n74ls48_6_f), .g(n74ls48_6_g));
  _7_Segment_Display u_7_segment_display_5 (
    .g(n74ls48_4_g), .f(n74ls48_4_f), .a(n74ls48_4_a_2), .b(n74ls48_4_b_2), .e(n74ls48_4_e),
    .d(n74ls48_4_d_2), .c(n74ls48_4_c_2));  // open: dp
  _7_Segment_Display u_7_segment_display_6 (
    .g(n74ls48_5_g), .f(n74ls48_5_f), .a(n74ls48_5_a_2), .b(n74ls48_5_b_2), .e(n74ls48_5_e),
    .d(n74ls48_5_d_2), .c(n74ls48_5_c_2));  // open: dp
  _7_Segment_Display u_7_segment_display_7 (
    .g(n74ls48_6_g), .f(n74ls48_6_f), .a(n74ls48_6_a_2), .b(n74ls48_6_b_2), .e(n74ls48_6_e),
    .d(n74ls48_6_d_2), .c(n74ls48_6_c_2));  // open: dp
endmodule

module _2 (
  input  in_1,
  input  in_2,
  input  [1:0] S,
  input  DL,
  input  DR,
  input  _3,
  input  _2,
  input  _1,
  input  _0,
  output Q3,
  output Q2,
  output Q1,
  output Q0
);

  wire not_1_out;
  wire [3:0] multiplexer_1_out;

  not not_1 (not_1_out, in_2);
  D_Flip_Flop d_ff_1 (.clk(in_1), .D(multiplexer_1_out[3]), .Q(Q3), .reset(not_1_out));  // open: Qn, preset, en
  Multiplexer #(.select(2), .width(4)) multiplexer_1 (
    .in0({_3, _2, _1, _0}), .in1({DR, Q3, Q2, Q1}), .in2({Q2, Q1, Q0, DL}), .in3({Q3, Q2, Q1, Q0}),
    .out(multiplexer_1_out), .sel(S));  // open: en
  D_Flip_Flop d_ff_2 (.clk(in_1), .D(multiplexer_1_out[2]), .Q(Q2), .reset(not_1_out));  // open: Qn, preset, en
  D_Flip_Flop d_ff_3 (.clk(in_1), .D(multiplexer_1_out[1]), .Q(Q1), .reset(not_1_out));  // open: Qn, preset, en
  D_Flip_Flop d_ff_4 (.clk(in_1), .D(multiplexer_1_out[0]), .Q(Q0), .reset(not_1_out));  // open: Qn, preset, en

  // Other names for the same wires on the sheet: S0[3:0] = {_3, _2, _1, _0}; S1[3:0] = {DR, Q3, Q2, Q1};
  //   S2[3:0] = {Q2, Q1, Q0, DL}; S3[3:0] = {Q3, Q2, Q1, Q0}
endmodule

module _2_2 (
  input  _3,
  input  _2,
  input  _1,
  input  _0
);

  wire n74ls48_1_a_2, n74ls48_1_b_2, n74ls48_1_c_2, n74ls48_1_d_2, n74ls48_1_e, n74ls48_1_f, n74ls48_1_g;

  _74LS48 u_74ls48_1 (
    .D(_3), .C(_2), .B(_1), .A(_0), .a_2(n74ls48_1_a_2), .b_2(n74ls48_1_b_2), .c_2(n74ls48_1_c_2),
    .d_2(n74ls48_1_d_2), .e(n74ls48_1_e), .f(n74ls48_1_f), .g(n74ls48_1_g));
  _7_Segment_Display u_7_segment_display_1 (
    .g(n74ls48_1_g), .f(n74ls48_1_f), .a(n74ls48_1_a_2), .b(n74ls48_1_b_2), .e(n74ls48_1_e),
    .d(n74ls48_1_d_2), .c(n74ls48_1_c_2));  // open: dp
  _7_Segment_Display u_7_segment_display_2 ();  // open: g, f, a, b, e, d, c, dp
endmodule

module _3 (
  input  D,
  input  C,
  input  B,
  input  A,
  output a_2,
  output b_2,
  output c_2,
  output d_2,
  output e,
  output f,
  output g
);

  wire and_1_out, and_2_out, and_3_out, and_4_out, and_5_out, and_6_out, and_7_out, and_8_out, and_9_out,
       and_10_out, and_11_out, and_12_out, and_13_out, and_14_out, and_15_out, and_16_out, and_17_out,
       and_18_out, and_19_out, and_20_out, and_21_out, and_22_out, and_23_out, and_24_out, and_25_out,
       and_26_out, and_27_out, and_28_out, and_29_out, and_30_out, and_31_out, and_32_out, and_33_out,
       and_34_out, and_35_out, not_1_out, not_2_out, not_3_out, not_4_out, not_5_out, not_6_out, not_7_out,
       not_8_out, not_9_out, not_10_out, not_11_out, not_12_out, not_13_out, not_14_out, not_15_out,
       not_16_out, not_17_out, not_18_out, not_19_out, not_20_out, not_21_out, not_22_out, not_23_out,
       not_24_out, not_25_out, not_26_out, not_27_out, not_28_out, not_29_out, not_30_out, not_31_out,
       not_32_out, not_33_out, not_34_out, not_35_out, not_36_out, not_37_out, not_38_out, not_39_out,
       not_40_out, not_41_out, not_42_out, not_43_out, not_44_out, not_45_out, not_46_out;

  not not_1 (not_1_out, C);
  and and_1 (and_1_out, not_1_out, not_2_out);
  not not_2 (not_2_out, A);
  not not_3 (not_3_out, D);
  and and_2 (and_2_out, not_3_out, B);
  not not_4 (not_4_out, D);
  and and_3 (and_3_out, not_4_out, C, A);
  and and_4 (and_4_out, C, B);
  not not_5 (not_5_out, C);
  and and_5 (and_5_out, D, not_5_out, not_6_out);
  not not_6 (not_6_out, B);
  and and_6 (and_6_out, D, not_7_out);
  not not_7 (not_7_out, A);
  not not_8 (not_8_out, D);
  and and_7 (and_7_out, not_8_out, not_9_out);
  not not_9 (not_9_out, C);
  not not_10 (not_10_out, D);
  and and_8 (and_8_out, not_10_out, not_11_out, not_12_out);
  not not_11 (not_11_out, B);
  not not_12 (not_12_out, A);
  not not_13 (not_13_out, C);
  and and_9 (and_9_out, not_13_out, not_14_out);
  not not_14 (not_14_out, A);
  not not_15 (not_15_out, D);
  and and_10 (and_10_out, not_15_out, B, A);
  and and_11 (and_11_out, D, not_16_out, A);
  not not_16 (not_16_out, B);
  not not_17 (not_17_out, D);
  and and_12 (and_12_out, not_17_out, not_18_out);
  not not_18 (not_18_out, B);
  not not_19 (not_19_out, D);
  and and_13 (and_13_out, not_19_out, A);
  not not_20 (not_20_out, B);
  and and_14 (and_14_out, not_20_out, A);
  not not_21 (not_21_out, D);
  and and_15 (and_15_out, not_21_out, C);
  and and_16 (and_16_out, D, not_22_out);
  not not_22 (not_22_out, C);
  not not_23 (not_23_out, D);
  not not_24 (not_24_out, C);
  and and_17 (and_17_out, not_23_out, not_24_out, not_25_out);
  not not_25 (not_25_out, A);
  not not_26 (not_26_out, D);
  and and_18 (and_18_out, not_26_out, B, not_27_out);
  not not_27 (not_27_out, A);
  not not_28 (not_28_out, C);
  and and_19 (and_19_out, not_28_out, B, A);
  not not_29 (not_29_out, B);
  and and_20 (and_20_out, C, not_29_out, A);
  and and_21 (and_21_out, D, not_30_out);
  not not_30 (not_30_out, B);
  and and_22 (and_22_out, D, C);
  not not_31 (not_31_out, C);
  and and_23 (and_23_out, not_31_out, not_32_out);
  not not_32 (not_32_out, A);
  and and_24 (and_24_out, B, not_33_out);
  not not_33 (not_33_out, A);
  not not_34 (not_34_out, C);
  and and_25 (and_25_out, D, not_34_out, B);
  and and_26 (and_26_out, D, C, not_35_out);
  not not_35 (not_35_out, B);
  not not_36 (not_36_out, B);
  and and_27 (and_27_out, not_36_out, not_37_out);
  not not_37 (not_37_out, A);
  not not_38 (not_38_out, D);
  and and_28 (and_28_out, not_38_out, C, not_39_out);
  not not_39 (not_39_out, B);
  and and_29 (and_29_out, C, not_40_out);
  not not_40 (not_40_out, A);
  and and_30 (and_30_out, D, not_41_out);
  not not_41 (not_41_out, C);
  not not_42 (not_42_out, C);
  and and_31 (and_31_out, not_42_out, B);
  and and_32 (and_32_out, B, not_43_out);
  not not_43 (not_43_out, A);
  not not_44 (not_44_out, D);
  and and_33 (and_33_out, not_44_out, C, not_45_out);
  not not_45 (not_45_out, B);
  and and_34 (and_34_out, D, not_46_out);
  not not_46 (not_46_out, C);
  and and_35 (and_35_out, D, A);
  or or_1 (b_2, and_7_out, and_8_out, and_9_out, and_10_out, and_11_out);
  or or_2 (c_2, and_12_out, and_13_out, and_14_out, and_15_out, and_16_out);
  or or_3 (e, and_23_out, and_24_out, and_25_out, and_26_out);
  or or_4 (f, and_27_out, and_28_out, and_29_out, and_30_out);
  or or_5 (g, and_31_out, and_32_out, and_33_out, and_34_out, and_35_out);
  or or_6 (a_2, and_1_out, and_2_out, and_3_out, and_4_out, and_5_out, and_6_out);
  or or_7 (d_2, and_17_out, and_18_out, and_19_out, and_20_out, and_21_out, and_22_out);
endmodule
