// Logisim project 0324.circ as structural Verilog
module main (
  input  in_1,
  output out_2,
  output out_3,
  output out_4,
  output out_5
);

  wire and_1_out, and_2_out, clock_1_out, mo5jsq_1_q0, mo5jsq_1_q1, mo5jsq_1_q2, mo5jsq_1_q3, mo5jsq_2_q0,
       mo5jsq_2_q1, mo5jsq_2_q2, mo5jsq_2_q3, n74ls48_1_a_2, n74ls48_1_b_2, n74ls48_1_c_2, n74ls48_1_d_2,
       n74ls48_1_e, n74ls48_1_f, n74ls48_1_g, n74ls48_2_a_2, n74ls48_2_b_2, n74ls48_2_c_2, n74ls48_2_d_2,
       n74ls48_2_e, n74ls48_2_f, n74ls48_2_g;

  and and_1 (and_1_out, mo5jsq_1_q1, mo5jsq_1_q0);
  _74LS48 u_74ls48_1 (
    .D(mo5jsq_1_q2), .C(mo5jsq_1_q1), .B(mo5jsq_1_q0), .A(mo5jsq_1_q3), .a_2(n74ls48_1_a_2),
    .b_2(n74ls48_1_b_2), .c_2(n74ls48_1_c_2), .d_2(n74ls48_1_d_2), .e(n74ls48_1_e), .f(n74ls48_1_f),
    .g(n74ls48_1_g));
  MO5JSQ mo5jsq_1 (
    .Q0(mo5jsq_1_q0), .Q1(mo5jsq_1_q1), .Q2(mo5jsq_1_q2), .Q3(mo5jsq_1_q3), .B(mo5jsq_1_q3), .A(and_2_out),
    ._9(1'b0), .in_1(and_1_out));
  _7_Segment_Display u_7_segment_display_1 (
    .g(n74ls48_1_g), .f(n74ls48_1_f), .a(n74ls48_1_a_2), .b(n74ls48_1_b_2), .e(n74ls48_1_e),
    .d(n74ls48_1_d_2), .c(n74ls48_1_c_2));  // open: dp
  and and_2 (and_2_out, mo5jsq_2_q3, mo5jsq_2_q2);
  MO5JSQ mo5jsq_2 (
    .Q0(mo5jsq_2_q0), .Q1(mo5jsq_2_q1), .Q2(mo5jsq_2_q2), .Q3(mo5jsq_2_q3), .B(mo5jsq_2_q3), .A(clock_1_out),
    ._9(1'b0), .in_1(and_1_out));
  MO5JSQ mo5jsq_3 (.Q0(out_3), .Q1(out_4), .Q2(out_5), .Q3(out_2), .B(out_2), .A(in_1), ._9(1'b0), .in_1(1'b0));
  _74LS48 u_74ls48_2 (
    .D(mo5jsq_2_q2), .C(mo5jsq_2_q1), .B(mo5jsq_2_q0), .A(mo5jsq_2_q3), .a_2(n74ls48_2_a_2),
    .b_2(n74ls48_2_b_2), .c_2(n74ls48_2_c_2), .d_2(n74ls48_2_d_2), .e(n74ls48_2_e), .f(n74ls48_2_f),
    .g(n74ls48_2_g));
  _7_Segment_Display u_7_segment_display_2 (
    .g(n74ls48_2_g), .f(n74ls48_2_f), .a(n74ls48_2_a_2), .b(n74ls48_2_b_2), .e(n74ls48_2_e),
    .d(n74ls48_2_d_2), .c(n74ls48_2_c_2));  // open: dp
  Clock clock_1 (.out(clock_1_out));
endmodule

module _74LS90 (
  input  CPA,
  input  CPB,
  output Q0,
  output Q1,
  output Q2,
  output Q3
);

  wire and_1_out, and_2_out, and_3_out, and_4_out, d_ff_1_q, d_ff_1_qn, d_ff_2_q, d_ff_2_qn, d_ff_3_q,
       d_ff_3_qn, d_ff_4_q, d_ff_4_qn;

  not not_1 (Q0, d_ff_1_q);
  D_Flip_Flop d_ff_1 (.clk(CPA), .D(and_1_out), .Q(d_ff_1_q), .Qn(d_ff_1_qn));  // open: preset, en, reset
  and and_1 (and_1_out, CPB, d_ff_1_qn);
  D_Flip_Flop d_ff_2 (.clk(d_ff_1_q), .D(and_2_out), .Q(d_ff_2_q), .Qn(d_ff_2_qn));  // open: preset, en, reset
  and and_2 (and_2_out, CPB, d_ff_2_qn);
  not not_2 (Q1, d_ff_2_q);
  D_Flip_Flop d_ff_3 (.clk(d_ff_2_q), .D(and_3_out), .Q(d_ff_3_q), .Qn(d_ff_3_qn));  // open: preset, en, reset
  and and_3 (and_3_out, CPB, d_ff_3_qn);
  not not_3 (Q2, d_ff_3_q);
  D_Flip_Flop d_ff_4 (.clk(d_ff_3_q), .D(and_4_out), .Q(d_ff_4_q), .Qn(d_ff_4_qn));  // open: preset, en, reset
  and and_4 (and_4_out, CPB, d_ff_4_qn);
  not not_4 (Q3, d_ff_4_q);
endmodule

module MO5JSQ (
  input  in_1,
  input  B,
  input  _9,
  input  A,
  output Q0,
  output Q1,
  output Q2,
  output Q3
);

  wire and_1_out, d_ff_1_q, d_ff_1_qn, nor_1_out, not_1_out, not_2_out, not_4_out, or_1_out, or_2_out;

  not not_1 (not_1_out, B);
  not not_2 (not_2_out, A);
  or or_1 (or_1_out, Q2, not_1_out);
  D_Flip_Flop d_ff_1 (.clk(not_2_out), .D(d_ff_1_qn), .Q(d_ff_1_q), .Qn(d_ff_1_qn), .reset(_9));  // open: preset, en
  J_K_Flip_Flop j_k_ff_1 (.J(1'b1), .clk(or_1_out), .K(1'b1), .Q(Q0), .reset(in_1));  // open: Qn, preset, en
  not not_3 (Q3, d_ff_1_q);
  not not_4 (not_4_out, Q0);
  J_K_Flip_Flop j_k_ff_2 (.J(1'b1), .clk(not_4_out), .K(1'b1), .Q(Q1), .reset(in_1));  // open: Qn, preset, en
  and and_1 (and_1_out, Q0, Q1);
  nor nor_1 (nor_1_out, and_1_out, Q2);
  or or_2 (or_2_out, nor_1_out, not_1_out);
  J_K_Flip_Flop j_k_ff_3 (.J(1'b1), .clk(or_2_out), .K(1'b1), .Q(Q2), .reset(in_1));  // open: Qn, preset, en
endmodule

module XIANSHI (
  input  _3,
  input  _2,
  input  _1,
  input  _0
);

  wire n74ls48_1_a_2, n74ls48_1_b_2, n74ls48_1_c_2, n74ls48_1_d_2, n74ls48_1_e, n74ls48_1_f, n74ls48_1_g;

  _74LS48 u_74ls48_1 (
    .D(_3), .C(_2), .B(_1), .A(_0), .a_2(n74ls48_1_a_2), .b_2(n74ls48_1_b_2), .c_2(n74ls48_1_c_2),
    .d_2(n74ls48_1_d_2), .e(n74ls48_1_e), .f(n74ls48_1_f), .g(n74ls48_1_g));
  _7_Segment_Display u_7_segment_display_1 (
    .g(n74ls48_1_g), .f(n74ls48_1_f), .a(n74ls48_1_a_2), .b(n74ls48_1_b_2), .e(n74ls48_1_e),
    .d(n74ls48_1_d_2), .c(n74ls48_1_c_2));  // open: dp
endmodule

module _74LS48 (
  input  D,
  input  C,
  input  B,
  input  A,
  output a_2,
  output b_2,
  output c_2,
  output d_2,
  output e,
  output f,
  output g
);

  wire and_1_out, and_2_out, and_3_out, and_4_out, and_5_out, and_6_out, and_7_out, and_8_out, and_9_out,
       and_10_out, and_11_out, and_12_out, and_13_out, and_14_out, and_15_out, and_16_out, and_17_out,
       and_18_out, and_19_out, and_20_out, and_21_out, and_22_out, and_23_out, and_24_out, and_25_out,
       and_26_out, and_27_out, not_1_out, not_2_out, not_3_out, not_4_out, not_5_out, not_6_out, not_7_out,
       not_8_out, not_9_out, not_10_out, not_11_out, not_12_out, not_13_out, not_14_out, not_15_out,
       not_16_out, not_17_out, not_18_out, not_19_out, not_20_out, not_21_out, not_22_out, not_23_out,
       not_24_out, not_25_out, not_26_out, not_27_out, not_28_out, not_29_out, not_30_out, not_31_out,
       not_32_out, not_33_out, not_34_out, not_35_out, not_36_out, not_37_out;

  not not_1 (not_1_out, D);
  and and_1 (and_1_out, not_1_out, not_2_out, not_3_out);
  not not_2 (not_2_out, C);
  not not_3 (not_3_out, A);
  not not_4 (not_4_out, D);
  and and_2 (and_2_out, not_4_out, not_5_out, B);
  not not_5 (not_5_out, C);
  not not_6 (not_6_out, D);
  and and_3 (and_3_out, not_6_out, C, A);
  not not_7 (not_7_out, C);
  and and_4 (and_4_out, D, not_7_out, not_8_out);
  not not_8 (not_8_out, B);
  and and_5 (and_5_out, D, not_9_out, A);
  not not_9 (not_9_out, B);
  not not_10 (not_10_out, D);
  and and_6 (and_6_out, not_10_out, not_11_out);
  not not_11 (not_11_out, C);
  not not_12 (not_12_out, C);
  and and_7 (and_7_out, not_12_out, not_13_out);
  not not_13 (not_13_out, B);
  not not_14 (not_14_out, B);
  and and_8 (and_8_out, not_14_out, not_15_out);
  not not_15 (not_15_out, A);
  and and_9 (and_9_out, C, B, A);
  not not_16 (not_16_out, C);
  and and_10 (and_10_out, not_16_out, not_17_out);
  not not_17 (not_17_out, B);
  not not_18 (not_18_out, B);
  and and_11 (and_11_out, not_18_out, not_19_out);
  not not_19 (not_19_out, A);
  and and_12 (and_12_out, B, A);
  not not_20 (not_20_out, D);
  and and_13 (and_13_out, not_20_out, C);
  not not_21 (not_21_out, C);
  and and_14 (and_14_out, not_21_out, not_22_out);
  not not_22 (not_22_out, A);
  not not_23 (not_23_out, C);
  and and_15 (and_15_out, not_23_out, B);
  and and_16 (and_16_out, B, not_24_out);
  not not_24 (not_24_out, A);
  and and_17 (and_17_out, C, not_25_out, A);
  not not_25 (not_25_out, B);
  not not_26 (not_26_out, C);
  and and_18 (and_18_out, not_26_out, not_27_out);
  not not_27 (not_27_out, A);
  and and_19 (and_19_out, B, not_28_out);
  not not_28 (not_28_out, A);
  not not_29 (not_29_out, B);
  and and_20 (and_20_out, not_29_out, not_30_out);
  not not_30 (not_30_out, A);
  and and_21 (and_21_out, C, not_31_out);
  not not_31 (not_31_out, B);
  and and_22 (and_22_out, C, not_32_out);
  not not_32 (not_32_out, A);
  and and_23 (and_23_out, D, not_33_out);
  not not_33 (not_33_out, B);
  not not_34 (not_34_out, C);
  and and_24 (and_24_out, not_34_out, B);
  and and_25 (and_25_out, C, not_35_out);
  not not_35 (not_35_out, B);
  and and_26 (and_26_out, C, not_36_out);
  not not_36 (not_36_out, A);
  and and_27 (and_27_out, D, not_37_out);
  not not_37 (not_37_out, C);
  or or_1 (a_2, and_1_out, and_2_out, and_3_out, and_4_out, and_5_out);
  or or_2 (b_2, and_6_out, and_7_out, and_8_out, and_9_out);
  or or_3 (c_2, and_10_out, and_11_out, and_12_out, and_13_out);
  or or_4 (d_2, and_14_out, and_15_out, and_16_out, and_17_out);
  or or_5 (e, and_18_out, and_19_out);
  or or_6 (f, and_20_out, and_21_out, and_22_out, and_23_out);
  or or_7 (g, and_24_out, and_25_out, and_26_out, and_27_out);
endmodule
