// Logisim project 03241.circ as structural Verilog: 9 circuits, main circuit main
module main (
  input  a3,
  input  a2,
  input  a1,
  input  a0,
  input  b3,
  input  b2,
  input  b1,
  input  b0,
  input  CLEAR,
  input  CLEAR_2,
  input  CLEAR_3,
  output y4,
  output y3,
  output y2,
  output y1,
  output y0
);

  wire _1HZ_out, and_1_out, and_2_out, and_3_out, and_4_out, and_5_out, and_6_out, and_7_out, and_8_out,
       button_1_out, button_2_out, n74ls48_1_p1, n74ls48_1_p2, n74ls48_1_p3, n74ls48_1_p4, n74ls48_1_p6,
       n74ls48_1_p8, n74ls48_1_p10, n74ls48_1_p12, n74ls48_1_p16, n74ls48_1_p17, n74ls48_1_p18, n74ls48_2_p6,
       n74ls48_2_p8, n74ls48_2_p10, n74ls48_2_p12, n74ls48_3_p1, n74ls48_3_p2, n74ls48_3_p3, n74ls48_3_p5,
       n74ls48_3_p7, n74ls48_3_p9, n74ls48_3_p11, n74ls48_3_p14, n74ls48_3_p15, n74ls48_3_p16, n74ls48_4_p5,
       n74ls48_4_p7, n74ls48_4_p9, n74ls48_4_p11, n74ls48_5_p1, n74ls48_5_p2, n74ls48_5_p3, n74ls48_5_p5,
       n74ls48_5_p7, n74ls48_5_p9, n74ls48_5_p11, n74ls48_5_p14, n74ls48_5_p15, n74ls48_5_p16, n74ls48_6_p5,
       n74ls48_6_p7, n74ls48_6_p9, n74ls48_6_p11, n74ls390_1__2qa, n74ls390_1__2qb, n74ls390_1__2qc,
       n74ls390_1__2qd, n74ls390_1_qa, n74ls390_1_qb, n74ls390_1_qc, n74ls390_1_qd, n74ls390_2__2qa,
       n74ls390_2__2qb, n74ls390_2__2qc, n74ls390_2__2qd, n74ls390_2_qa, n74ls390_2_qb, n74ls390_2_qc,
       n74ls390_2_qd, n74ls390_3__2qa, n74ls390_3__2qb, n74ls390_3__2qc, n74ls390_3__2qd, n74ls390_3_qa,
       n74ls390_3_qb, n74ls390_3_qc, n74ls390_3_qd, or_1_out, or_2_out, or_3_out, or_5_out, or_6_out;

  QJQ qjq_1 (
    .a3(a3), .a2(a2), .a1(a1), .a0(a0), .b3(b3), .b2(b2), .b1(b1), .b0(b0), .out_9(y4), .out_10(y3),
    .out_11(y2), .out_12(y1), .out_13(y0));
  and and_1 (and_1_out, n74ls390_1__2qa, ~n74ls390_1__2qb, ~n74ls390_1__2qc, n74ls390_1__2qd);  // AND_Gate
  or or_1 (or_1_out, CLEAR, and_2_out);
  _74LS390 u_74ls390_1 (
    .B(n74ls390_1_qa), .CLEAR(or_1_out), ._2B(n74ls390_1__2qa), ._2A(n74ls48_1_p3), ._2CLEAR(or_2_out),
    .QA(n74ls390_1_qa), .QB(n74ls390_1_qb), .QC(n74ls390_1_qc), .QD(n74ls390_1_qd), ._2QA(n74ls390_1__2qa),
    ._2QB(n74ls390_1__2qb), ._2QC(n74ls390_1__2qc), ._2QD(n74ls390_1__2qd), .A(and_1_out));
  and and_2 (and_2_out, and_3_out, and_4_out);
  or or_2 (or_2_out, and_2_out, CLEAR);
  and and_3 (and_3_out, ~n74ls390_1_qa, n74ls390_1_qb, ~n74ls390_1_qc, ~n74ls390_1_qd);  // AND_Gate
  _7_Segment_Display u_7_segment_display_1 (
    .g(n74ls48_2_p12), .f(n74ls48_2_p10), .a(n74ls48_1_p16), .b(n74ls48_1_p17), .e(n74ls48_2_p8),
    .d(n74ls48_2_p6), .c(n74ls48_1_p18));  // open: dp
  _7_Segment_Display u_7_segment_display_2 (
    .g(n74ls48_1_p12), .f(n74ls48_1_p10), .a(n74ls48_1_p1), .b(n74ls48_1_p2), .e(n74ls48_1_p8),
    .d(n74ls48_1_p6), .c(n74ls48_1_p4));  // open: dp
  // _74LS48 74ls48_1: pin names not known; wires that end beside it: n74ls48_1_p1, n74ls48_1_p2, n74ls48_1_p3, n74ls48_1_p4, n74ls390_1_qd, n74ls48_1_p6, n74ls390_1_qc, n74ls48_1_p8, n74ls390_1_qb, n74ls48_1_p10, n74ls390_1_qa, n74ls48_1_p12, n74ls48_1_p3, n74ls390_1__2qa, n74ls390_1__2qd, n74ls48_1_p16, n74ls48_1_p17, n74ls48_1_p18
  // _74LS48 74ls48_2: pin names not known; wires that end beside it: n74ls48_1_p16, n74ls48_1_p17, n74ls48_1_p3, n74ls48_1_p18, n74ls390_1__2qd, n74ls48_2_p6, n74ls390_1__2qc, n74ls48_2_p8, n74ls390_1__2qb, n74ls48_2_p10, n74ls390_1__2qa, n74ls48_2_p12, n74ls48_1_p3
  and and_4 (and_4_out, ~n74ls390_1__2qd, n74ls390_1__2qc, ~n74ls390_1__2qb, ~n74ls390_1__2qa);  // AND_Gate
  and and_5 (and_5_out, n74ls390_2__2qa, ~n74ls390_2__2qb, ~n74ls390_2__2qc, n74ls390_2__2qd);  // AND_Gate
  or or_3 (or_3_out, CLEAR_2, and_6_out);
  or or_4 (n74ls48_1_p3, button_1_out, and_6_out);
  Button button_1 (.out(button_1_out));
  _74LS390 u_74ls390_2 (
    .B(n74ls390_2_qa), .CLEAR(or_3_out), ._2B(n74ls390_2__2qa), ._2A(or_5_out), ._2CLEAR(CLEAR_2),
    .QA(n74ls390_2_qa), .QB(n74ls390_2_qb), .QC(n74ls390_2_qc), .QD(n74ls390_2_qd), ._2QA(n74ls390_2__2qa),
    ._2QB(n74ls390_2__2qb), ._2QC(n74ls390_2__2qc), ._2QD(n74ls390_2__2qd), .A(and_5_out));
  and and_6 (and_6_out, ~n74ls390_2_qa, n74ls390_2_qb, n74ls390_2_qc, ~n74ls390_2_qd);  // AND_Gate
  _7_Segment_Display u_7_segment_display_3 (
    .g(n74ls48_3_p11), .f(n74ls48_3_p9), .a(n74ls48_3_p1), .b(n74ls48_3_p2), .e(n74ls48_3_p7),
    .d(n74ls48_3_p5), .c(n74ls48_3_p3));  // open: dp
  _7_Segment_Display u_7_segment_display_4 (
    .g(n74ls48_4_p11), .f(n74ls48_4_p9), .a(n74ls48_3_p14), .b(n74ls48_3_p15), .e(n74ls48_4_p7),
    .d(n74ls48_4_p5), .c(n74ls48_3_p16));  // open: dp
  // _74LS48 74ls48_3: pin names not known; wires that end beside it: n74ls48_3_p1, n74ls48_3_p2, n74ls48_3_p3, n74ls390_2_qd, n74ls48_3_p5, n74ls390_2_qc, n74ls48_3_p7, n74ls390_2_qb, n74ls48_3_p9, n74ls390_2_qa, n74ls48_3_p11, n74ls390_2__2qa, n74ls390_2__2qd, n74ls48_3_p14, n74ls48_3_p15, n74ls48_3_p16
  // _74LS48 74ls48_4: pin names not known; wires that end beside it: n74ls48_3_p14, n74ls48_3_p15, n74ls48_3_p16, n74ls390_2__2qd, n74ls48_4_p5, n74ls390_2__2qc, n74ls48_4_p7, n74ls390_2__2qb, n74ls48_4_p9, n74ls390_2__2qa, n74ls48_4_p11
  or or_5 (or_5_out, button_2_out, and_8_out);
  Button button_2 (.out(button_2_out));
  or or_6 (or_6_out, CLEAR_3, and_8_out);
  and and_7 (and_7_out, n74ls390_3__2qa, ~n74ls390_3__2qb, ~n74ls390_3__2qc, n74ls390_3__2qd);  // AND_Gate
  _74LS390 u_74ls390_3 (
    .B(n74ls390_3_qa), .CLEAR(or_6_out), ._2B(n74ls390_3__2qa), ._2A(_1HZ_out), ._2CLEAR(CLEAR_3),
    .QA(n74ls390_3_qa), .QB(n74ls390_3_qb), .QC(n74ls390_3_qc), .QD(n74ls390_3_qd), ._2QA(n74ls390_3__2qa),
    ._2QB(n74ls390_3__2qb), ._2QC(n74ls390_3__2qc), ._2QD(n74ls390_3__2qd), .A(and_7_out));
  Clock _1HZ (.out(_1HZ_out));
  and and_8 (and_8_out, ~n74ls390_3_qa, n74ls390_3_qb, n74ls390_3_qc, ~n74ls390_3_qd);  // AND_Gate
  _7_Segment_Display u_7_segment_display_5 (
    .g(n74ls48_5_p11), .f(n74ls48_5_p9), .a(n74ls48_5_p1), .b(n74ls48_5_p2), .e(n74ls48_5_p7),
    .d(n74ls48_5_p5), .c(n74ls48_5_p3));  // open: dp
  _7_Segment_Display u_7_segment_display_6 (
    .g(n74ls48_6_p11), .f(n74ls48_6_p9), .a(n74ls48_5_p14), .b(n74ls48_5_p15), .e(n74ls48_6_p7),
    .d(n74ls48_6_p5), .c(n74ls48_5_p16));  // open: dp
  // _74LS48 74ls48_5: pin names not known; wires that end beside it: n74ls48_5_p1, n74ls48_5_p2, n74ls48_5_p3, n74ls390_3_qd, n74ls48_5_p5, n74ls390_3_qc, n74ls48_5_p7, n74ls390_3_qb, n74ls48_5_p9, n74ls390_3_qa, n74ls48_5_p11, n74ls390_3__2qa, n74ls390_3__2qd, n74ls48_5_p14, n74ls48_5_p15, n74ls48_5_p16
  // _74LS48 74ls48_6: pin names not known; wires that end beside it: n74ls48_5_p14, n74ls48_5_p15, n74ls48_5_p16, n74ls390_3__2qd, n74ls48_6_p5, n74ls390_3__2qc, n74ls48_6_p7, n74ls390_3__2qb, n74ls48_6_p9, n74ls390_3__2qa, n74ls48_6_p11

  // Notes on the sheet:
  //   时钟（24）
  //   分钟（60）
  //   秒钟（60）
endmodule

module _74LS90 (
  input  A,
  input  B,
  input  R0,
  input  R9,
  output QA,
  output QB,
  output QC,
  output QD
);

  wire and_1_out, nQD, or_1_out;

  or or_1 (or_1_out, R0, R9);
  J_K_Flip_Flop #(.trigger("falling")) j_k_ff_1 (
    .J(1'b1), .clk(A), .K(1'b1), .Q(QA), .preset(R9), .reset(R0));  // open: Qn, en
  J_K_Flip_Flop #(.trigger("falling")) j_k_ff_2 (
    .J(nQD), .clk(B), .K(1'b1), .Q(QB), .reset(or_1_out));  // open: Qn, preset, en
  J_K_Flip_Flop #(.trigger("falling")) j_k_ff_3 (
    .J(QB), .clk(B), .K(QB), .Q(QC), .reset(or_1_out));  // open: Qn, preset, en
  and and_1 (and_1_out, QC, QB);
  J_K_Flip_Flop #(.trigger("falling")) j_k_ff_4 (
    .J(and_1_out), .clk(B), .K(QD), .Q(QD), .Qn(nQD), .preset(R9), .reset(R0));  // open: en

  // Notes on the sheet:
  //   置0
  //   置9
endmodule

module _74LS390 (
  input  B,
  input  A,
  input  CLEAR,
  input  _2B,
  input  _2A,
  input  _2CLEAR,
  output QA,
  output QB,
  output QC,
  output QD,
  output _2QA,
  output _2QB,
  output _2QC,
  output _2QD
);

  _74LS90 u_74ls90_1 (.A(A), .B(B), .R0(CLEAR), .QA(QA), .QB(QB), .QC(QC), .QD(QD));  // open: R9
  _74LS90 u_74ls90_2 (.A(_2A), .B(_2B), .R0(_2CLEAR), .QA(_2QA), .QB(_2QB), .QC(_2QC), .QD(_2QD));  // open: R9
endmodule

module _74LS48 (
  input  D,
  input  C,
  input  B,
  input  A,
  output Ya,
  output Yb,
  output Yc,
  output Yd,
  output Ye,
  output Yf,
  output Yg,
  output Yh
);

  wire and_1_out, and_2_out, and_3_out, and_4_out, and_5_out, and_6_out, and_7_out, and_8_out, and_9_out,
       and_10_out, and_11_out, and_12_out, and_13_out, and_14_out, and_15_out, and_16_out, and_17_out,
       and_18_out, and_19_out, and_20_out, and_21_out, and_22_out, and_23_out, and_24_out, and_25_out,
       and_26_out, and_27_out, and_28_out, and_29_out, and_30_out, and_31_out, and_32_out, and_33_out,
       not_1_out, not_2_out, not_3_out, not_4_out, not_5_out, not_6_out, not_7_out, not_8_out, not_9_out,
       not_10_out, not_11_out, not_12_out, not_13_out, not_14_out, not_15_out, not_16_out, not_17_out,
       not_18_out, not_19_out, not_20_out, not_21_out, not_22_out, not_23_out, not_24_out, not_25_out,
       not_26_out, not_27_out, not_28_out, not_29_out, not_30_out, not_31_out, not_32_out, not_33_out,
       not_34_out, not_35_out, not_36_out, not_37_out, not_38_out, not_39_out, not_40_out, not_41_out,
       not_42_out, not_43_out;

  not not_1 (not_1_out, C);
  and and_1 (and_1_out, not_1_out, not_2_out);
  not not_2 (not_2_out, A);
  not not_3 (not_3_out, D);
  and and_2 (and_2_out, not_3_out, B);
  and and_3 (and_3_out, C, A);
  and and_4 (and_4_out, D, not_4_out);
  not not_4 (not_4_out, B);
  not not_5 (not_5_out, C);
  not not_6 (not_6_out, B);
  and and_5 (and_5_out, not_6_out, not_7_out);
  not not_7 (not_7_out, A);
  not not_8 (not_8_out, D);
  and and_6 (and_6_out, not_8_out, B, A);
  and and_7 (and_7_out, D, not_9_out);
  not not_9 (not_9_out, B);
  and and_8 (and_8_out, D, not_10_out);
  not not_10 (not_10_out, A);
  not not_11 (not_11_out, D);
  and and_9 (and_9_out, not_11_out, not_12_out);
  not not_12 (not_12_out, B);
  and and_10 (and_10_out, C, B);
  and and_11 (and_11_out, D, not_13_out);
  not not_13 (not_13_out, C);
  not not_14 (not_14_out, C);
  and and_12 (and_12_out, not_14_out, not_15_out);
  not not_15 (not_15_out, A);
  not not_16 (not_16_out, D);
  not not_17 (not_17_out, C);
  and and_13 (and_13_out, not_16_out, not_17_out, B);
  not not_18 (not_18_out, D);
  and and_14 (and_14_out, not_18_out, B, not_19_out);
  not not_19 (not_19_out, A);
  not not_20 (not_20_out, B);
  and and_15 (and_15_out, C, not_20_out, A);
  and and_16 (and_16_out, D, not_21_out);
  not not_21 (not_21_out, B);
  and and_17 (and_17_out, D, C, A);
  not not_22 (not_22_out, C);
  and and_18 (and_18_out, not_22_out, not_23_out);
  not not_23 (not_23_out, A);
  not not_24 (not_24_out, D);
  and and_19 (and_19_out, not_24_out, B, not_25_out);
  not not_25 (not_25_out, A);
  and and_20 (and_20_out, D, not_26_out, not_27_out);
  not not_26 (not_26_out, B);
  not not_27 (not_27_out, A);
  not not_28 (not_28_out, D);
  and and_21 (and_21_out, not_28_out, not_29_out, not_30_out);
  not not_29 (not_29_out, B);
  not not_30 (not_30_out, A);
  not not_31 (not_31_out, D);
  and and_22 (and_22_out, not_31_out, C, not_32_out);
  not not_32 (not_32_out, B);
  not not_33 (not_33_out, D);
  and and_23 (and_23_out, not_33_out, C, not_34_out);
  not not_34 (not_34_out, A);
  and and_24 (and_24_out, D, not_35_out, not_36_out);
  not not_35 (not_35_out, C);
  not not_36 (not_36_out, B);
  not not_37 (not_37_out, C);
  and and_25 (and_25_out, D, not_37_out, not_38_out);
  not not_38 (not_38_out, A);
  and and_26 (and_26_out, D, C, B);
  not not_39 (not_39_out, D);
  and and_27 (and_27_out, not_39_out, not_40_out, B);
  not not_40 (not_40_out, C);
  and and_28 (and_28_out, C, not_41_out);
  not not_41 (not_41_out, B);
  and and_29 (and_29_out, C, not_42_out);
  not not_42 (not_42_out, A);
  and and_30 (and_30_out, D, not_43_out);
  not not_43 (not_43_out, B);
  and and_31 (and_31_out, D, C);
  and and_32 (and_32_out, D, B);
  and and_33 (and_33_out, D, C);
  or or_1 (Ya, and_1_out, and_2_out, and_3_out, and_4_out);
  or or_2 (Yb, not_5_out, and_5_out, and_6_out, and_7_out, and_8_out);
  or or_3 (Yc, and_9_out, A, and_10_out, and_11_out);
  or or_4 (Ye, and_18_out, and_19_out, and_20_out);
  or or_5 (Yg, and_27_out, and_28_out, and_29_out, and_30_out, and_31_out);
  or or_6 (Yh, and_32_out, and_33_out);
  or or_7 (Yd, and_12_out, and_13_out, and_14_out, and_15_out, and_16_out, and_17_out);
  or or_8 (Yf, and_21_out, and_22_out, and_23_out, and_24_out, and_25_out, and_26_out);
endmodule

module mowujishuqi (
  input  in_1,
  input  B,
  input  A,
  input  in_4,
  output Q3,
  output Q0,
  output Q1,
  output Q2
);

  wire and_1_out, nor_1_out, not_1_out, not_2_out, or_1_out, or_2_out;

  not not_1 (not_1_out, B);
  or or_1 (or_1_out, Q2, not_1_out);
  J_K_Flip_Flop #(.trigger("falling")) j_k_ff_1 (
    .J(1'b1), .clk(A), .K(1'b1), .Q(Q3), .preset(in_4), .reset(in_1));  // open: Qn, en
  J_K_Flip_Flop j_k_ff_2 (.J(1'b1), .clk(or_1_out), .K(1'b1), .Q(Q0), .reset(in_1));  // open: Qn, preset, en
  J_K_Flip_Flop j_k_ff_3 (.J(1'b1), .clk(not_2_out), .K(1'b1), .Q(Q1), .reset(in_1));  // open: Qn, preset, en
  not not_2 (not_2_out, Q0);
  and and_1 (and_1_out, Q0, Q1);
  nor nor_1 (nor_1_out, and_1_out, Q2);
  or or_2 (or_2_out, nor_1_out, not_1_out);
  J_K_Flip_Flop j_k_ff_4 (.J(1'b1), .clk(or_2_out), .K(1'b1), .Q(Q2), .reset(in_1));  // open: Qn, preset, en
endmodule

module QJQ (
  input  a3,
  input  a2,
  input  a1,
  input  a0,
  input  b3,
  input  b2,
  input  b1,
  input  b0,
  output out_9,
  output out_10,
  output out_11,
  output out_12,
  output out_13
);

  wire n22_1_cout, n22_2_cout, n22_3_cout;

  _22 u_22_1 (.A(a0), .B(b0), .cin(1'b0), .out(out_13), .cout(n22_1_cout));
  _22 u_22_2 (.A(a1), .B(b1), .cin(n22_1_cout), .out(out_12), .cout(n22_2_cout));
  _22 u_22_3 (.A(a2), .B(b2), .cin(n22_2_cout), .out(out_11), .cout(n22_3_cout));
  _22 u_22_4 (.A(a3), .B(b3), .cin(n22_3_cout), .out(out_10), .cout(out_9));
endmodule

module _22 (
  input  A,
  input  B,
  input  cin,
  output out,
  output cout
);

  wire and_1_out, and_2_out, and_3_out, and_4_out, and_5_out, and_6_out, and_7_out, not_1_out, not_2_out,
       not_3_out, not_4_out, not_5_out, not_6_out;

  not not_1 (not_1_out, A);
  not not_2 (not_2_out, B);
  not not_3 (not_3_out, A);
  not not_4 (not_4_out, cin);
  not not_5 (not_5_out, B);
  not not_6 (not_6_out, cin);
  and and_1 (and_1_out, B, cin);
  and and_2 (and_2_out, A, cin);
  and and_3 (and_3_out, A, B);
  and and_4 (and_4_out, not_1_out, not_2_out, cin);
  and and_5 (and_5_out, not_3_out, B, not_4_out);
  and and_6 (and_6_out, A, not_5_out, not_6_out);
  and and_7 (and_7_out, A, B, cin);
  or or_1 (cout, and_1_out, and_2_out, and_3_out);
  or or_2 (out, and_4_out, and_5_out, and_6_out, and_7_out);
endmodule

module qjq2 (
  input  a3,
  input  a2,
  input  a1,
  input  a0,
  input  b3,
  input  b2,
  input  b1,
  input  b0,
  output y4,
  output y3,
  output y2,
  output y1,
  output y0
);

  QJQ qjq_1 (
    .a3(a3), .a2(a2), .a1(a1), .a0(a0), .b3(b3), .b2(b2), .b1(b1), .b0(b0), .out_9(y4), .out_10(y3),
    .out_11(y2), .out_12(y1), .out_13(y0));
endmodule

module clock (
  input  in_1
);

  wire _1, _1f, _1h, _2, _2f, _2h, _3, _3f, _3h, _4, _4f, _4h, a, a1, af, af1, ah, ah1, and_1_out, and_2_out,
       and_3_out, and_5_out, and_7_out, b, b1, bf, bf1, bh, bh1, button_1_out, button_2_out, c, c1, cf, cf1,
       ch, ch1, clock_1_out, d, d1, df, df1, dh, dh1, e, e1, ef, ef1, eh, eh1, f, f1, f2, f3, f4, ff, ff1,
       fff1, fh, fh1, fu1, g, g1, gf, gf1, gh, gh1, hhh1, m1, m2, m3, m4, mmm1, nf, nh, nm, shi1, shi2, shi3,
       shi4, w1, w2;

  _7_Segment_Display u_7_segment_display_1 (.g(gh1), .f(fh1), .a(ah1), .b(bh1), .e(eh1), .d(dh1), .c(ch1), .dp(1'b0));
  and and_1 (and_1_out, m3, m2);
  and and_2 (and_2_out, shi2, _3h);
  and and_3 (and_3_out, f3, f2);
  or or_1 (mmm1, in_1, and_1_out);
  or or_2 (hhh1, in_1, and_2_out);
  or or_3 (fff1, in_1, and_3_out);
  _7_Segment_Display u_7_segment_display_2 (.g(gh), .f(fh), .a(ah), .b(bh), .e(eh), .d(dh), .c(ch), .dp(1'b1));
  _74LS48 u_74ls48_1 (
    .D(shi4), .C(shi3), .B(shi2), .A(shi1), .Ya(ah1), .Yb(bh1), .Yc(ch1), .Yd(dh1), .Ye(eh1), .Yf(fh1),
    .Yg(gh1));  // open: Yh
  _74LS48 u_74ls48_2 (
    .D(_4h), .C(_3h), .B(_2h), .A(_1h), .Ya(ah), .Yb(bh), .Yc(ch), .Yd(dh), .Ye(eh), .Yf(fh), .Yg(gh));  // open: Yh
  _74LS390 u_74ls390_1 (
    .B(shi1), .CLEAR(hhh1), ._2B(_1h), ._2A(w2), ._2CLEAR(hhh1), .QA(shi1), .QB(shi2), .QC(shi3), .QD(shi4),
    ._2QA(_1h), ._2QB(_2h), ._2QC(_3h), ._2QD(_4h), .A(nh));
  _7_Segment_Display u_7_segment_display_3 (.g(gf1), .f(ff1), .a(af1), .b(bf1), .e(ef1), .d(df1), .c(cf1), .dp(1'b0));
  and and_4 (nh, _1h, ~_2h, ~_3h, _4h);  // AND_Gate
  _74LS48 u_74ls48_3 (
    .D(f4), .C(f3), .B(f2), .A(fu1), .Ya(af1), .Yb(bf1), .Yc(cf1), .Yd(df1), .Ye(ef1), .Yf(ff1), .Yg(gf1));  // open: Yh
  Button button_1 (.out(button_1_out));
  _7_Segment_Display u_7_segment_display_4 (.g(gf), .f(ff), .a(af), .b(bf), .e(ef), .d(df), .c(cf), .dp(1'b1));
  _74LS390 u_74ls390_2 (
    .B(fu1), .CLEAR(fff1), ._2B(_1f), ._2A(w1), ._2CLEAR(fff1), .QA(fu1), .QB(f2), .QC(f3), .QD(f4),
    ._2QA(_1f), ._2QB(_2f), ._2QC(_3f), ._2QD(_4f), .A(nf));
  and and_5 (and_5_out, ~fu1, f2, f3, ~f4);  // AND_Gate
  or or_4 (w2, and_5_out, button_1_out);
  _74LS48 u_74ls48_4 (
    .D(_4f), .C(_3f), .B(_2f), .A(_1f), .Ya(af), .Yb(bf), .Yc(cf), .Yd(df), .Ye(ef), .Yf(ff), .Yg(gf));  // open: Yh
  and and_6 (nf, _1f, ~_2f, ~_3f, _4f);  // AND_Gate
  Button button_2 (.out(button_2_out));
  and and_7 (and_7_out, ~m1, m2, m3, ~m4);  // AND_Gate
  _7_Segment_Display u_7_segment_display_5 (.g(g1), .f(f1), .a(a1), .b(b1), .e(e1), .d(d1), .c(c1), .dp(1'b0));
  _74LS48 u_74ls48_5 (
    .D(m4), .C(m3), .B(m2), .A(m1), .Ya(a1), .Yb(b1), .Yc(c1), .Yd(d1), .Ye(e1), .Yf(f1), .Yg(g1));  // open: Yh
  _74LS390 u_74ls390_3 (
    .B(m1), .CLEAR(mmm1), ._2B(_1), ._2A(clock_1_out), ._2CLEAR(mmm1), .QA(m1), .QB(m2), .QC(m3), .QD(m4),
    ._2QA(_1), ._2QB(_2), ._2QC(_3), ._2QD(_4), .A(nm));
  or or_5 (w1, and_7_out, button_2_out);
  and and_8 (nm, _1, ~_2, ~_3, _4);  // AND_Gate
  _7_Segment_Display u_7_segment_display_6 (.g(g), .f(f), .a(a), .b(b), .e(e), .d(d), .c(c), .dp(1'b0));
  _74LS48 u_74ls48_6 (
    .D(_4), .C(_3), .B(_2), .A(_1), .Ya(a), .Yb(b), .Yc(c), .Yd(d), .Ye(e), .Yf(f), .Yg(g));  // open: Yh
  Clock clock_1 (.out(clock_1_out));

  // Other names for the same wires on the sheet: fff2 = fff1; hhh2 = hhh1; mmm2 = mmm1; sssf = in_1; sssh = in_1;
  //   sssm = in_1

  // Notes on the sheet:
  //   时钟（24）
  //   分钟（60）
  //   秒钟（60）
endmodule
