// Logisim project 数字逻辑四位全加器.circ as structural Verilog: 3 circuits, main circuit main
module main (
  input  a3,
  input  a2,
  input  a1,
  input  a0,
  input  b3,
  input  b2,
  input  b1,
  input  b0,
  output y4,
  output y3,
  output y2,
  output y1,
  output y0
);

  \全加器  \u_全加器_1  (
    .a3(a3), .a2(a2), .a1(a1), .a0(a0), .b3(b3), .b2(b2), .b1(b1), .b0(b0), .out_9(y4), .out_10(y3),
    .out_11(y2), .out_12(y1), .out_13(y0));
endmodule

module \二位加法器  (
  input  A,
  input  B,
  input  cin,
  output out,
  output cout
);

  wire and_1_out, and_2_out, and_3_out, and_4_out, and_5_out, and_6_out, and_7_out, not_1_out, not_2_out,
       not_3_out, not_4_out, not_5_out, not_6_out;

  not not_1 (not_1_out, A);
  and and_1 (and_1_out, not_1_out, not_2_out, cin);
  not not_2 (not_2_out, B);
  not not_3 (not_3_out, A);
  and and_2 (and_2_out, not_3_out, B, not_4_out);
  not not_4 (not_4_out, cin);
  not not_5 (not_5_out, B);
  and and_3 (and_3_out, A, not_5_out, not_6_out);
  not not_6 (not_6_out, cin);
  and and_4 (and_4_out, A, B, cin);
  and and_5 (and_5_out, B, cin);
  and and_6 (and_6_out, A, cin);
  and and_7 (and_7_out, A, B);
  or or_1 (out, and_1_out, and_2_out, and_3_out, and_4_out);
  or or_2 (cout, and_5_out, and_6_out, and_7_out);
endmodule

module \全加器  (
  input  a3,
  input  a2,
  input  a1,
  input  a0,
  input  b3,
  input  b2,
  input  b1,
  input  b0,
  output out_9,
  output out_10,
  output out_11,
  output out_12,
  output out_13
);

  wire \二位加法器_1_cout , \二位加法器_2_cout , \二位加法器_3_cout ;

  \二位加法器  \u_二位加法器_1  (.A(a0), .B(b0), .cin(1'b0), .out(out_13), .cout(\二位加法器_1_cout ));
  \二位加法器  \u_二位加法器_2  (.A(a1), .B(b1), .cin(\二位加法器_1_cout ), .out(out_12), .cout(\二位加法器_2_cout ));
  \二位加法器  \u_二位加法器_3  (.A(a2), .B(b2), .cin(\二位加法器_2_cout ), .out(out_11), .cout(\二位加法器_3_cout ));
  \二位加法器  \u_二位加法器_4  (.A(a3), .B(b3), .cin(\二位加法器_3_cout ), .out(out_10), .cout(out_9));
endmodule
