// Logisim project 2-2022211477-王有强-八条模型机.circ as structural Verilog: 6 circuits, main circuit time02
module main (
  input  in_1,
  output [7:0] out_2,
  output [2:0] out_3
);

  wire A_minus, A_plus, CLA, CLK, controlled_buffer_3_out, controlled_buffer_4_out, controlled_buffer_7_out,
       controlled_buffer_12_out, controlled_buffer_13_out, controlled_buffer_15_out, EX, FE, JMP, L1, L2, LG,
       MG, not_1_out, or_1_out, or_3_out, or_4_out, or_5_out, P1, P2, P3, P4, RST, SHR, STP, T0, T1, T2, T3,
       X_minus, X_plus;
  wire [4:4] IR_q;
  wire [7:0] AD_IR, adder_1_out, BUS, controlled_buffer_1_out, controlled_buffer_2_out,
       controlled_buffer_10_out, controlled_buffer_11_out, controlled_buffer_14_out,
       controlled_buffer_16_out, controlled_buffer_18_out, controlled_buffer_19_out, cun, MAR_q, MDR_q,
       multiplexer_1_out, PC_q, register_1_q, register_2_q, register_3_q, shr_1_out_2, subtractor_1_out;

  Clock clock_1 (.out(CLK));
  time04 time04_1 (.Clock(CLK), .RSet(RST), .T0(T0), .T1(T1), .T2(T2), .T3(T3));
  assign controlled_buffer_1_out = LG ? AD_IR : 8'bz;  // Controlled_Buffer controlled_buffer_1
  \微指令发生器  \u_微指令发生器_1  (
    .PC_MAR(P1), .MdR_X(X_plus), .cla(CLA), .M1(MG), .M_GATE(LG), .MDR_IR(P4), .MdR_ACC(L2),
    .ACC_plus(A_plus), .MdR_X_2(X_minus), .PC_1(P3), .jmp(JMP), .ACC_minus(A_minus), .ad_mar(L1),
    .MAR_MDR(P2), .stop(STP), .shr(SHR), .in_1(T0), .in_2(T1), .in_7(out_3), .in_3(T2), .in_4(T3), .in_5(FE),
    .in_6(EX));
  assign controlled_buffer_2_out = or_1_out ? multiplexer_1_out : 8'bz;  // Controlled_Buffer controlled_buffer_2
  Multiplexer #(.width(8), .enable("false")) multiplexer_1 (
    .in0(BUS), .in1(controlled_buffer_1_out), .out(multiplexer_1_out), .sel(MG));
  or or_1 (or_1_out, P1, L1);
  time02 time02_1 (.in_1(T3), .in_2(RST), .out_3(FE), .out_4(EX));
  Register MAR (.D(controlled_buffer_2_out), .Q(MAR_q), .clk(controlled_buffer_3_out), .clr(RST));  // open: en
  assign controlled_buffer_3_out = or_1_out ? CLK : 1'bz;  // Controlled_Buffer controlled_buffer_3
  or or_2 (RST, in_1, STP);
  RAM ram_1 (.addr(MAR_q), .data(cun), .clk(T3), .ld(not_1_out));  // open: sel, clr
  not not_1 (not_1_out, MG);
  Register MDR (.D(cun), .Q(MDR_q), .clk(controlled_buffer_4_out), .clr(RST));  // open: en
  assign controlled_buffer_4_out = P2 ? CLK : 1'bz;  // Controlled_Buffer controlled_buffer_4
  assign out_2 = P3 ? BUS : 8'bz;  // Controlled_Buffer controlled_buffer_5
  assign BUS = or_3_out ? MDR_q : 8'bz;  // Controlled_Buffer controlled_buffer_6
  or or_3 (or_3_out, P3, X_plus, L2, X_minus);
  Register IR (.D(out_2), .Q({out_3, IR_q[4], AD_IR[3:0]}), .clk(controlled_buffer_7_out), .clr(RST));  // open: en
  assign controlled_buffer_7_out = P3 ? CLK : 1'bz;  // Controlled_Buffer controlled_buffer_7
  assign AD_IR[7:4] = LG ? 4'b1010 : 4'bz;  // Controlled_Buffer controlled_buffer_8
  assign AD_IR[7:4] = JMP ? 4'b0001 : 4'bz;  // Controlled_Buffer controlled_buffer_9
  assign controlled_buffer_10_out = X_plus ? BUS : 8'bz;  // Controlled_Buffer controlled_buffer_10
  assign controlled_buffer_11_out = or_4_out ? BUS : 8'bz;  // Controlled_Buffer controlled_buffer_11
  or or_4 (or_4_out, SHR, A_plus, L2, A_minus);
  assign controlled_buffer_12_out = X_plus ? CLK : 1'bz;  // Controlled_Buffer controlled_buffer_12
  assign controlled_buffer_13_out = or_4_out ? CLK : 1'bz;  // Controlled_Buffer controlled_buffer_13
  assign controlled_buffer_14_out = X_minus ? BUS : 8'bz;  // Controlled_Buffer controlled_buffer_14
  assign controlled_buffer_15_out = X_minus ? CLK : 1'bz;  // Controlled_Buffer controlled_buffer_15
  Register register_1 (
    .D(controlled_buffer_10_out), .Q(register_1_q), .clk(controlled_buffer_12_out), .clr(RST));  // open: en
  Register register_2 (
    .D(controlled_buffer_11_out), .Q(register_2_q), .clk(controlled_buffer_13_out), .clr(or_5_out));  // open: en
  or or_5 (or_5_out, RST, CLA);
  Register register_3 (
    .D(controlled_buffer_14_out), .Q(register_3_q), .clk(controlled_buffer_15_out), .clr(RST));  // open: en
  assign controlled_buffer_16_out = JMP ? AD_IR : 8'bz;  // Controlled_Buffer controlled_buffer_16
  assign cun = MG ? register_2_q : 8'bz;  // Controlled_Buffer controlled_buffer_17
  assign controlled_buffer_18_out = SHR ? register_2_q : 8'bz;  // Controlled_Buffer controlled_buffer_18
  assign controlled_buffer_19_out = A_minus ? register_2_q : 8'bz;  // Controlled_Buffer controlled_buffer_19
  Counter PC (.load(JMP), .D(controlled_buffer_16_out), .count(P4), .Q(PC_q), .clk(CLK), .clr(RST));  // open: carry
  assign BUS = P1 ? PC_q : 8'bz;  // Controlled_Buffer controlled_buffer_20
  Hex_Digit_Display hex_digit_display_1 (.value(register_2_q[7:4]));  // open: dp
  Adder adder_1 (.a(register_1_q), .b(register_2_q), .out(adder_1_out));  // open: cin, cout
  SHR shr_1 (.out_2(shr_1_out_2), .in_1(controlled_buffer_18_out));
  Subtractor subtractor_1 (.a(controlled_buffer_19_out), .b(register_3_q), .out(subtractor_1_out));  // open: bin, bout
  Hex_Digit_Display hex_digit_display_2 (.value(register_2_q[3:0]));  // open: dp
  assign BUS = A_plus ? adder_1_out : 8'bz;  // Controlled_Buffer controlled_buffer_21
  assign BUS = L1 ? AD_IR : 8'bz;  // Controlled_Buffer controlled_buffer_22
  assign BUS = SHR ? shr_1_out_2 : 8'bz;  // Controlled_Buffer controlled_buffer_23
  assign BUS = A_minus ? subtractor_1_out : 8'bz;  // Controlled_Buffer controlled_buffer_24

  // Other names for the same wires on the sheet: OP[2:0] = out_3

  // Notes on the sheet:
  //   时序状态模块
  //   主存
  //   微指令发生器
  //   IR
  //   00  000  LDA
  //   20  001  ADD
  //   40  010  SUB
  //   60  011  STA
  //   80 100  SHR
  //   A0  101  CLA
  //   C0  110  JMP
  //   E0  111  STP
  //   ACC
  //   程序计数器
  //   传值
endmodule

module time02 (
  input  in_1,
  input  in_2,
  output out_3,
  output out_4
);

  D_Flip_Flop #(.trigger("falling")) d_ff_1 (.clk(in_1), .D(out_4), .Q(out_3), .preset(in_2));  // open: Qn, en, reset
  D_Flip_Flop #(.trigger("falling")) d_ff_2 (.clk(in_1), .D(out_3), .Q(out_4), .reset(in_2));  // open: Qn, preset, en
endmodule

module time03 (
  input  Clock,
  input  RSet,
  output T0,
  output T1,
  output T2
);

  D_Flip_Flop #(.trigger("falling")) d_ff_1 (.clk(Clock), .D(T2), .Q(T0), .preset(RSet));  // open: Qn, en, reset
  D_Flip_Flop #(.trigger("falling")) d_ff_2 (.clk(Clock), .D(T0), .Q(T1), .reset(RSet));  // open: Qn, preset, en
  D_Flip_Flop #(.trigger("falling")) d_ff_3 (.clk(Clock), .D(T1), .Q(T2), .reset(RSet));  // open: Qn, preset, en
endmodule

module time04 (
  input  Clock,
  input  RSet,
  output T0,
  output T1,
  output T2,
  output T3
);

  D_Flip_Flop #(.trigger("falling")) d_ff_1 (.clk(Clock), .D(T3), .Q(T0), .preset(RSet));  // open: Qn, en, reset
  D_Flip_Flop #(.trigger("falling")) d_ff_2 (.clk(Clock), .D(T0), .Q(T1), .reset(RSet));  // open: Qn, preset, en
  D_Flip_Flop #(.trigger("falling")) d_ff_3 (.clk(Clock), .D(T1), .Q(T2), .reset(RSet));  // open: Qn, preset, en
  D_Flip_Flop #(.trigger("falling")) d_ff_4 (.clk(Clock), .D(T2), .Q(T3), .reset(RSet));  // open: Qn, preset, en
endmodule

module \微指令发生器  (
  input  in_1,
  input  in_2,
  input  in_3,
  input  in_4,
  input  in_5,
  input  in_6,
  input  [2:0] in_7,
  output MAR_MDR,
  output PC_MAR,
  output MDR_IR,
  output PC_1,
  output MdR_X,
  output ACC_plus,
  output jmp,
  output stop,
  output cla,
  output MdR_X_2,
  output ACC_minus,
  output shr,
  output M1,
  output MdR_ACC,
  output ad_mar,
  output M_GATE
);

  wire ADD, and_11_out, and_12_out, CLA_t, JMP_t, LDA, or_1_out, or_3_out, or_4_out, SHR_t, STA, STOP_t, SUB;

  Decoder #(.select(3), .enable("false")) decoder_1 (
    .out0(LDA), .out1(ADD), .out2(SUB), .out3(STA), .out4(SHR_t), .out5(CLA_t), .out6(JMP_t), .out7(STOP_t),
    .sel(in_7));
  and and_1 (PC_MAR, in_5, in_1);
  and and_2 (MdR_X, in_6, ADD, in_3);
  and and_3 (cla, in_6, CLA_t, in_4);
  and and_4 (M1, in_6, STA);
  and and_5 (M_GATE, in_6, or_1_out);
  and and_6 (MDR_IR, in_5, in_3);
  or or_1 (or_1_out, STA, LDA, ADD, SUB);
  and and_7 (PC_1, in_5, in_4);
  and and_8 (ACC_plus, in_6, ADD, in_4);
  and and_9 (MdR_X_2, in_6, SUB, in_3);
  and and_10 (MdR_ACC, in_6, LDA, in_3);
  or or_2 (MAR_MDR, and_11_out, and_12_out);
  and and_11 (and_11_out, in_5, in_2);
  and and_12 (and_12_out, in_6, or_3_out, in_2);
  and and_13 (jmp, in_6, JMP_t, in_3);
  and and_14 (ACC_minus, in_6, SUB, in_4);
  and and_15 (ad_mar, in_6, or_4_out, in_1);
  or or_3 (or_3_out, LDA, SUB, ADD);
  and and_16 (stop, in_6, STOP_t, in_4);
  and and_17 (shr, in_6, SHR_t, in_2);
  or or_4 (or_4_out, STA, LDA, ADD, SUB);

  // Other names for the same wires on the sheet: EX = in_6; FE = in_5; T0 = in_1; T1 = in_2; T2 = in_3; T3 = in_4
endmodule

module SHR (
  input  [7:0] in_1,
  output [7:0] out_2
);

  // Probe on in_1[0]

  assign out_2 = {1'b0, in_1[7:1]};
endmodule
