// Logisim project 2022211477-王有强-01-寄存器实验.circ as structural Verilog: 7 circuits, main circuit main
module main (
  input  [7:0] in_1,
  input  AEN,
  input  WEN,
  input  SA,
  input  SB
);

  wire clock_1_out, R0, R1, R2, R3;
  wire [7:0] controlled_buffer_1_out, register_2_q, register_4_q, \右移电路_1_out_2 , \左移电路_1_out_2 ,
       \直传电路_1_out_2 ;

  Clock clock_1 (.out(clock_1_out));
  \左移电路  \u_左移电路_1  (.out_2(\左移电路_1_out_2 ), .in_1(controlled_buffer_1_out));
  Register #(.trigger("falling")) register_1 (.D(\左移电路_1_out_2 ), .clk(clock_1_out));  // open: en, Q, clr
  \直传电路  \u_直传电路_1  (.out_2(\直传电路_1_out_2 ), .in_1(controlled_buffer_1_out));
  assign controlled_buffer_1_out = AEN ? register_2_q : 8'bz;  // Controlled_Buffer controlled_buffer_1
  Register register_2 (.D(in_1), .en(AEN), .Q(register_2_q), .clk(clock_1_out));  // open: clr
  Register #(.trigger("falling")) register_3 (.D(\直传电路_1_out_2 ), .clk(clock_1_out));  // open: en, Q, clr
  \右移电路  \u_右移电路_1  (.out_2(\右移电路_1_out_2 ), .in_1(controlled_buffer_1_out));
  Register register_4 (.D(in_1), .en(WEN), .Q(register_4_q), .clk(clock_1_out));  // open: clr
  Register #(.trigger("falling")) register_5 (.D(\右移电路_1_out_2 ), .clk(clock_1_out));  // open: en, Q, clr
  assign controlled_buffer_1_out = WEN ? register_4_q : 8'bz;  // Controlled_Buffer controlled_buffer_2
  \选择电路  \u_选择电路_1  (._0_3(R2), ._0(R0), ._0_2(R1), ._0_4(R3), .SA(SA), .SB(SB));
  Register u_R0 (.D(in_1), .en(R0), .clk(clock_1_out));  // open: Q, clr
  Register u_R1 (.D(in_1), .en(R1), .clk(clock_1_out));  // open: Q, clr
  Register u_R2 (.D(in_1), .en(R2), .clk(clock_1_out));  // open: Q, clr
  Register u_R3 (.D(in_1), .en(R3), .clk(clock_1_out));  // open: Q, clr

  // Notes on the sheet:
  //   L
  //   A
  //   D
  //   R
  //   W
endmodule

module \直传电路  (
  input  [7:0] in_1,
  output [7:0] out_2
);


  assign out_2 = in_1;
endmodule

module \左移电路  (
  input  [7:0] in_1,
  output [7:0] out_2
);


  assign out_2 = {in_1[6:0], 1'b0};
endmodule

module \右移电路  (
  input  [7:0] in_1,
  output [7:0] out_2
);


  assign out_2 = {1'b0, in_1[7:1]};
endmodule

module \选择电路  (
  input  SA,
  input  SB,
  output _0,
  output _0_2,
  output _0_3,
  output _0_4
);

  Decoder #(.select(2)) decoder_1 (.out0(_0), .out1(_0_2), .out2(_0_3), .out3(_0_4), .sel({SB, SA}));  // open: en
endmodule

module \寄存器使用示例  (
  input  [7:0] in_1,
  input  in_2,
  input  in_3
);

  wire clock_1_out;
  wire [3:0] register_1_q, register_1_q_2;

  Clock clock_1 (.out(clock_1_out));
  Hex_Digit_Display hex_digit_display_1 (.value(register_1_q_2));  // open: dp
  Register #(.trigger("falling")) register_1 (
    .D(in_1), .en(in_2), .Q({register_1_q_2, register_1_q}), .clk(clock_1_out), .clr(in_3));
  Hex_Digit_Display hex_digit_display_2 (.value(register_1_q));  // open: dp

  // Notes on the sheet:
  //   高端
  //   Enable(使能端)
  //   时钟触发方式
  //   四种触发方式
  //   清0端
endmodule

module \总线连接模式示例  (
  input  [7:0] \公用输入端 ,
  input  Reset,
  input  AEN,
  input  WEN
);

  wire clock_1_out;
  wire [3:0] controlled_buffer_1_out, controlled_buffer_1_out_2;
  wire [7:0] A_q, W_q;

  Clock clock_1 (.out(clock_1_out));
  assign {controlled_buffer_1_out_2, controlled_buffer_1_out} = AEN ? A_q : 8'bz;  // Controlled_Buffer controlled_buffer_1
  Register A (.D(\公用输入端 ), .en(AEN), .Q(A_q), .clk(clock_1_out), .clr(Reset));
  Hex_Digit_Display hex_digit_display_1 (.value(controlled_buffer_1_out_2));  // open: dp
  Hex_Digit_Display hex_digit_display_2 (.value(controlled_buffer_1_out));  // open: dp
  Register W (.D(\公用输入端 ), .en(WEN), .Q(W_q), .clk(clock_1_out), .clr(Reset));
  assign {controlled_buffer_1_out_2, controlled_buffer_1_out} = WEN ? W_q : 8'bz;  // Controlled_Buffer controlled_buffer_2

  // Notes on the sheet:
  //   可控三态门
endmodule
