// Logisim project 2022211477-王有强-设计文件-3.circ as structural Verilog: 4 circuits, main circuit main
module main (
  input  [7:0] \输入端 ,
  input  [7:0] \输入端_2 ,
  input  RAM_W,
  input  Reset,
  input  [7:0] \输入端_3 
);

  wire CLK, not_1_out, T0, T1;
  wire [3:0] MDR_2_q, MDR_2_q_2, ram_2_data, ram_2_data_2;
  wire [7:0] MAR_2_q, MAR_q, MDR_q, ram_1_data;

  Clock clock_1 (.out(CLK));
  Time_03 time_03_1 (.Clock(CLK), .RSet(Reset), .T0(T0), .T1(T1));  // open: T2
  Register #(.trigger("falling")) MAR (.D(\输入端 ), .en(T0), .Q(MAR_q), .clk(CLK), .clr(Reset));
  RAM ram_1 (.addr(MAR_q), .data(ram_1_data));  // open: sel, clk, ld, clr
  Register MAR_2 (.D(\输入端_2 ), .en(T0), .Q(MAR_2_q), .clk(CLK), .clr(Reset));
  Register MDR (.D(\输入端_3 ), .en(T1), .Q(MDR_q), .clk(CLK), .clr(Reset));
  Register #(.trigger("falling")) MDR_2 (.D(ram_1_data), .en(T1), .Q({MDR_2_q_2, MDR_2_q}), .clk(CLK), .clr(Reset));
  Hex_Digit_Display hex_digit_display_1 (.value(MDR_2_q_2));  // open: dp
  RAM ram_2 (.addr(MAR_2_q), .data({ram_2_data_2, ram_2_data}), .clk(CLK), .ld(RAM_W));  // open: sel, clr
  not not_1 (not_1_out, RAM_W);
  Hex_Digit_Display hex_digit_display_2 (.value(MDR_2_q));  // open: dp
  assign {ram_2_data_2, ram_2_data} = not_1_out ? MDR_q : 8'bz;  // Controlled_Buffer controlled_buffer_1
  Hex_Digit_Display hex_digit_display_3 (.value(ram_2_data_2));  // open: dp
  Hex_Digit_Display hex_digit_display_4 (.value(ram_2_data));  // open: dp

  // Other names for the same wires on the sheet: RST = Reset
endmodule

module Time_03 (
  input  Clock,
  input  RSet,
  output T0,
  output T1,
  output T2
);

  D_Flip_Flop d_ff_1 (.clk(Clock), .D(T2), .Q(T0), .preset(RSet));  // open: Qn, en, reset
  D_Flip_Flop d_ff_2 (.clk(Clock), .D(T0), .Q(T1), .reset(RSet));  // open: Qn, preset, en
  D_Flip_Flop d_ff_3 (.clk(Clock), .D(T1), .Q(T2), .reset(RSet));  // open: Qn, preset, en

  // Notes on the sheet:
  //   CLK
  //   T0
  //   T1
  //   T2
  //   时序关系示意图
endmodule

module \存储器读数示例  (
  input  [7:0] \输入端 ,
  input  MAR_W,
  input  MDR_W
);

  wire CLK;
  wire [3:0] MDR_q, MDR_q_2;
  wire [7:0] MAR_q, ram_1_data;

  Clock u_CLK (.out(CLK));
  Register MAR (.D(\输入端 ), .en(MAR_W), .Q(MAR_q), .clk(CLK));  // open: clr
  RAM ram_1 (.addr(MAR_q), .data(ram_1_data));  // open: sel, clk, ld, clr
  Hex_Digit_Display hex_digit_display_1 (.value(MDR_q_2));  // open: dp
  Register MDR (.D(ram_1_data), .en(MDR_W), .Q({MDR_q_2, MDR_q}), .clk(CLK));  // open: clr
  Hex_Digit_Display hex_digit_display_2 (.value(MDR_q));  // open: dp
endmodule

module \存储器写数示例  (
  input  [7:0] \输入端 ,
  input  MAR_W,
  input  RAM_W,
  input  MDR_W
);

  wire CLK, not_1_out;
  wire [7:0] MAR_q, MDR_q, ram_1_data;

  Clock u_CLK (.out(CLK));
  Register MAR (.D(\输入端 ), .en(MAR_W), .Q(MAR_q), .clk(CLK));  // open: clr
  Register MDR (.D(\输入端 ), .en(MDR_W), .Q(MDR_q), .clk(CLK));  // open: clr
  RAM ram_1 (.addr(MAR_q), .data(ram_1_data), .clk(CLK), .ld(RAM_W));  // open: sel, clr
  not not_1 (not_1_out, RAM_W);
  assign ram_1_data = not_1_out ? MDR_q : 8'bz;  // Controlled_Buffer controlled_buffer_1
  Hex_Digit_Display hex_digit_display_1 (.value(ram_1_data[7:4]));  // open: dp
  Hex_Digit_Display hex_digit_display_2 (.value(ram_1_data[3:0]));  // open: dp
endmodule
