// Logisim project 乘法矩阵.circ as structural Verilog: 4 circuits, main circuit main
module main (
  input  [3:0] X,
  input  [3:0] Y,
  output [7:0] out_3
);

  wire not_2_out, rx, ry, y0, y1, y2;
  wire [2:0] x_t;
  wire [3:1] jiafaqi_2_out_4, jiafaqi_3_out_4;
  wire [5:0] R0;
  wire [6:0] adder_1_out, not_1_out;

  xuanze xuanze_1 (.in_1(X), .out_2(x_t), .out_3(rx));
  xuanze xuanze_2 (.in_1(Y), .out_2({y2, y1, y0}), .out_3(ry));
  assign not_1_out = ~{1'b0, R0};  // NOT_Gate not_1, 7 bits wide
  Adder #(.width(7)) adder_1 (.a(7'b0000001), .b(not_1_out), .out(adder_1_out));  // open: cin, cout
  xor xor_1 (out_3[7], rx, ry);
  Multiplexer #(.width(7)) multiplexer_1 (
    .in0(adder_1_out), .in1({1'b0, R0}), .out(out_3[6:0]), .sel(not_2_out));  // open: en
  not not_2 (not_2_out, out_3[7]);
  jiafaqi jiafaqi_1 (.in_2(y2), .in_3(x_t), .out_4(R0[5:2]), .in_1({jiafaqi_2_out_4, R0[1]}));
  jiafaqi jiafaqi_2 (.in_2(y1), .in_3(x_t), .out_4({jiafaqi_2_out_4, R0[1]}), .in_1({jiafaqi_3_out_4, R0[0]}));
  jiafaqi jiafaqi_3 (.in_2(y0), .in_3(x_t), .out_4({jiafaqi_3_out_4, R0[0]}), .in_1(4'b0000));
endmodule

module xuanze (
  input  [3:0] in_1,
  output [2:0] out_2,
  output out_3
);

  wire not_2_out;
  wire [2:0] adder_1_out, not_1_out;

  assign not_1_out = ~in_1[2:0];  // NOT_Gate not_1, 3 bits wide
  Comparator #(.width(1), .mode("unsigned")) comparator_1 (.a(in_1[3]), .b(1'b1), .eq(out_3));  // open: gt, lt
  Adder #(.width(3)) adder_1 (.a(3'b001), .b(not_1_out), .out(adder_1_out));  // open: cin, cout
  Multiplexer #(.width(3)) multiplexer_1 (
    .in0(adder_1_out), .in1(in_1[2:0]), .out(out_2), .sel(not_2_out));  // open: en
  not not_2 (not_2_out, out_3);
endmodule

module jiafaqi (
  input  [3:0] in_1,
  input  in_2,
  input  [2:0] in_3,
  output [3:0] out_4
);

  wire and_1_out, and_2_out, and_3_out, n2j_1_cout, n2j_2_cout;

  and and_1 (and_1_out, in_2, in_3[0]);
  and and_2 (and_2_out, in_2, in_3[1]);
  and and_3 (and_3_out, in_3[2], in_2);
  _2j u_2j_1 (.A(in_1[1]), .B(and_1_out), .cin(1'b0), .out(out_4[0]), .cout(n2j_1_cout));
  _2j u_2j_2 (.A(in_1[2]), .B(and_2_out), .cin(n2j_1_cout), .out(out_4[1]), .cout(n2j_2_cout));
  _2j u_2j_3 (.A(in_1[3]), .B(and_3_out), .cin(n2j_2_cout), .out(out_4[2]), .cout(out_4[3]));
endmodule

module _2j (
  input  A,
  input  B,
  input  cin,
  output out,
  output cout
);

  wire and_1_out, and_2_out, and_3_out, and_4_out, and_5_out, and_6_out, and_7_out, not_1_out, not_2_out,
       not_3_out, not_4_out, not_5_out, not_6_out;

  not not_1 (not_1_out, A);
  not not_2 (not_2_out, B);
  not not_3 (not_3_out, A);
  not not_4 (not_4_out, cin);
  not not_5 (not_5_out, B);
  not not_6 (not_6_out, cin);
  and and_1 (and_1_out, B, cin);
  and and_2 (and_2_out, A, cin);
  and and_3 (and_3_out, A, B);
  and and_4 (and_4_out, not_1_out, not_2_out, cin);
  and and_5 (and_5_out, not_3_out, B, not_4_out);
  and and_6 (and_6_out, A, not_5_out, not_6_out);
  and and_7 (and_7_out, A, B, cin);
  or or_1 (cout, and_1_out, and_2_out, and_3_out);
  or or_2 (out, and_4_out, and_5_out, and_6_out, and_7_out);
endmodule
