// Logisim project 组成原理实验04_数据通路实验.circ as structural Verilog: 7 circuits, main circuit main
module main (
);


  // Notes on the sheet:
  //   要求：自己设计一个复杂的电路
  //   1、第一拍给地址、第二拍读出的数据送入寄存器、第三拍寄存器数据送入R0
endmodule

module \指令01  (
  input  [7:0] in_1,
  input  in_2
);

  wire clock_1_out, T0, time_02_1_t1;
  wire [7:0] ACC_q, controlled_buffer_1_out, controlled_buffer_2_out;

  Clock clock_1 (.out(clock_1_out));
  LED led_1 (.in(T0));
  Time_02 time_02_1 (.Clock(clock_1_out), .RSet(in_2), .T0(T0), .T1(time_02_1_t1));
  assign controlled_buffer_1_out = T0 ? in_1 : 8'bz;  // Controlled_Buffer controlled_buffer_1
  LED led_2 (.in(time_02_1_t1));
  assign controlled_buffer_2_out = T0 ? controlled_buffer_1_out : 8'bz;  // Controlled_Buffer controlled_buffer_2
  Register #(.trigger("falling")) ACC (.D(controlled_buffer_2_out), .Q(ACC_q), .clk(T0), .clr(in_2));  // open: en
  Hex_Digit_Display hex_digit_display_1 (.value(ACC_q[7:4]));  // open: dp
  Hex_Digit_Display hex_digit_display_2 (.value(ACC_q[3:0]));  // open: dp

  // Other names for the same wires on the sheet: RST = in_2

  // Notes on the sheet:
  //   向寄存器里送数据
  //   1、可控缓冲门
  //   2、寄存器写入脉冲（下沿）
endmodule

module \指令02  (
  input  [7:0] in_1,
  input  in_2
);

  wire CLK, controlled_buffer_3_out, or_1_out, or_2_out, T0, T1, undriven, undriven_2, undriven_3,
       undriven_4, undriven_5, undriven_6;
  wire [7:0] ACC_q, controlled_buffer_1_out, controlled_buffer_2_out, R0_q;

  Clock clock_1 (.out(CLK));
  LED led_1 (.in(T0));
  Time_02 time_02_1 (.Clock(CLK), .RSet(in_2), .T0(T0), .T1(T1));
  assign controlled_buffer_1_out = undriven ? in_1 : 8'bz;  // Controlled_Buffer controlled_buffer_1
  LED led_2 (.in(T1));
  assign controlled_buffer_2_out = or_1_out ? controlled_buffer_1_out : 8'bz;  // Controlled_Buffer controlled_buffer_2
  or or_1 (or_1_out, undriven_2, undriven_3);
  Register #(.trigger("falling")) ACC (
    .D(controlled_buffer_2_out), .Q(ACC_q), .clk(controlled_buffer_3_out), .clr(in_2));  // open: en
  assign controlled_buffer_3_out = or_2_out ? CLK : 1'bz;  // Controlled_Buffer controlled_buffer_3
  or or_2 (or_2_out, undriven_4, undriven_5);
  Register #(.trigger("falling")) R0 (.Q(R0_q), .clr(in_2));  // open: D, en, clk
  assign controlled_buffer_1_out = undriven_6 ? R0_q : 8'bz;  // Controlled_Buffer controlled_buffer_4
  Hex_Digit_Display hex_digit_display_1 (.value(ACC_q[7:4]));  // open: dp
  Hex_Digit_Display hex_digit_display_2 (.value(ACC_q[3:0]));  // open: dp

  // Other names for the same wires on the sheet: RST = in_2

  // Notes on the sheet:
  //   两拍分别向寄存器里送数据
  //   2、写入脉冲（下沿）控制
  //   1、节拍控制（第一拍数据直接送入寄存器、第二拍R0的数据送入）
endmodule

module \指令03  (
  input  [7:0] in_1,
  input  in_2
);

  wire CLK, T0, T1, undriven, undriven_2, undriven_3, undriven_4, undriven_5, undriven_6, undriven_7,
       undriven_8;
  wire [7:0] ACC_q, controlled_buffer_1_out, controlled_buffer_2_out, controlled_buffer_3_out, MAR_q,
       ram_1_data;

  Clock clock_1 (.out(CLK));
  LED led_1 (.in(T0));
  assign controlled_buffer_1_out = undriven ? in_1 : 8'bz;  // Controlled_Buffer controlled_buffer_1
  Time_02 time_02_1 (.Clock(CLK), .RSet(in_2), .T0(T0), .T1(T1));
  LED led_2 (.in(T1));
  assign controlled_buffer_2_out = undriven_2 ? controlled_buffer_1_out : 8'bz;  // Controlled_Buffer controlled_buffer_2
  assign controlled_buffer_3_out = undriven_3 ? controlled_buffer_1_out : 8'bz;  // Controlled_Buffer controlled_buffer_3
  Register #(.trigger("falling")) MAR (
    .D(controlled_buffer_2_out), .Q(MAR_q), .clk(undriven_4), .clr(undriven_5));  // open: en
  Register #(.trigger("falling")) ACC (
    .D(controlled_buffer_3_out), .Q(ACC_q), .clk(undriven_6), .clr(undriven_7));  // open: en
  Hex_Digit_Display hex_digit_display_1 (.value(ACC_q[7:4]));  // open: dp
  Hex_Digit_Display hex_digit_display_2 (.value(ACC_q[3:0]));  // open: dp
  RAM ram_1 (.addr(MAR_q), .data(ram_1_data));  // open: sel, clk, ld, clr
  assign controlled_buffer_1_out = undriven_8 ? ram_1_data : 8'bz;  // Controlled_Buffer controlled_buffer_4

  // Other names for the same wires on the sheet: RST = in_2

  // Notes on the sheet:
  //   两拍分别向寄存器里送数据
  //   2、写入脉冲（下沿）控制
  //   1、节拍控制（第一拍给地址、第二拍存储器读出的数据送入寄存器）
endmodule

module Time_04 (
  input  Clock,
  input  RSet,
  output T0,
  output T1,
  output T2,
  output T3
);

  D_Flip_Flop d_ff_1 (.clk(Clock), .D(T3), .Q(T0), .preset(RSet));  // open: Qn, en, reset
  D_Flip_Flop d_ff_2 (.clk(Clock), .D(T0), .Q(T1), .reset(RSet));  // open: Qn, preset, en
  D_Flip_Flop d_ff_3 (.clk(Clock), .D(T1), .Q(T2), .reset(RSet));  // open: Qn, preset, en
  D_Flip_Flop d_ff_4 (.clk(Clock), .D(T2), .Q(T3), .reset(RSet));  // open: Qn, preset, en
endmodule

module Time_03 (
  input  Clock,
  input  RSet,
  output T0,
  output T1,
  output T2
);

  D_Flip_Flop d_ff_1 (.clk(Clock), .D(T2), .Q(T0), .preset(RSet));  // open: Qn, en, reset
  D_Flip_Flop d_ff_2 (.clk(Clock), .D(T0), .Q(T1), .reset(RSet));  // open: Qn, preset, en
  D_Flip_Flop d_ff_3 (.clk(Clock), .D(T1), .Q(T2), .reset(RSet));  // open: Qn, preset, en

  // Notes on the sheet:
  //   CLK
  //   T0
  //   T1
  //   T2
  //   时序关系示意图
endmodule

module Time_02 (
  input  Clock,
  input  RSet,
  output T0,
  output T1
);

  D_Flip_Flop d_ff_1 (.clk(Clock), .D(T1), .Q(T0), .preset(RSet));  // open: Qn, en, reset
  D_Flip_Flop d_ff_2 (.clk(Clock), .D(T0), .Q(T1), .reset(RSet));  // open: Qn, preset, en
endmodule
