// Logisim project 补码时序.circ as structural Verilog: 5 circuits, main circuit main
module main (
  input  [7:0] in_1,
  output [7:0] X,
  output [7:0] Y
);

  wire clock_1_out, comparator_1_lt, controlled_buffer_1_out, Qn_1, RST, youyi1_1_out_3, youyi2_1_out_4;
  wire [7:0] counter_1_q, xuanze_1_out_4, youyi1_1_out_2, youyi2_1_out_3;
  wire [8:0] jiafaqi_1_out_3;
  wire [8:8] youyi1_1_out_2_2;

  Button u_RST (.out(RST));
  youyi1 youyi1_1 (.out_3(youyi1_1_out_3), .out_2({youyi1_1_out_2_2[8], youyi1_1_out_2}), .in_1(jiafaqi_1_out_3));
  Register ACC (.D(youyi1_1_out_2), .Q(X), .clk(controlled_buffer_1_out), .clr(RST));  // open: en
  jiafaqi jiafaqi_1 (.out_3(jiafaqi_1_out_3), .in_1(X), .in_2(xuanze_1_out_4));  // open: out_4
  xuanze xuanze_1 (.in_1(in_1), .out_4(xuanze_1_out_4), .in_2(Y[0]), .in_3(Qn_1));
  youyi2 youyi2_1 (.in_1(youyi1_1_out_3), .out_3(youyi2_1_out_3), .out_4(youyi2_1_out_4), .in_2(Y));
  Register MQ (.D(youyi2_1_out_3), .Q(Y), .clk(controlled_buffer_1_out), .clr(RST));  // open: en
  D_Flip_Flop d_ff_1 (
    .clk(controlled_buffer_1_out), .D(youyi2_1_out_4), .Q(Qn_1), .reset(RST));  // open: Qn, preset, en
  assign controlled_buffer_1_out = comparator_1_lt ? clock_1_out : 1'bz;  // Controlled_Buffer controlled_buffer_1
  Counter counter_1 (.D(8'h1), .Q(counter_1_q), .clk(clock_1_out), .clr(RST));  // open: load, count, carry
  Comparator #(.mode("unsigned")) comparator_1 (.a(counter_1_q), .b(8'h8), .lt(comparator_1_lt));  // open: gt, eq
  LED led_1 (.in(comparator_1_lt));
  Clock clock_1 (.out(clock_1_out));

  // Other names for the same wires on the sheet: ACC[7:0] = X; MQ[7:0] = Y; Qn = Y[0]
endmodule

module youyi1 (
  input  [8:0] in_1,
  output [8:0] out_2,
  output out_3
);


  assign out_2 = {{2{in_1[8]}}, in_1[7:1]};
  assign out_3 = in_1[0];
endmodule

module youyi2 (
  input  in_1,
  input  [7:0] in_2,
  output [7:0] out_3,
  output out_4
);


  assign out_3 = {in_1, in_2[7:1]};
  assign out_4 = in_2[0];
endmodule

module jiafaqi (
  input  [7:0] in_1,
  input  [7:0] in_2,
  output [8:0] out_3,
  output out_4
);

  Adder #(.width(9)) adder_1 (
    .a({{2{in_1[7]}}, in_1[6:0]}), .b({{2{in_2[7]}}, in_2[6:0]}), .out(out_3), .cout(out_4));  // open: cin
endmodule

module xuanze (
  input  [7:0] in_1,
  input  in_2,
  input  in_3,
  output [7:0] out_4
);

  wire A;
  wire [6:0] C, not_2_out, tunnel;
  wire [7:0] tunnel_t;

  Multiplexer #(.width(7)) multiplexer_1 (.in0(in_1[6:0]), .in1(C), .out(tunnel), .sel(A));  // open: en
  Multiplexer #(.width(7)) multiplexer_2 (
    .in0(in_1[6:0]), .in1(C), .out(tunnel_t[6:0]), .sel(tunnel_t[7]));  // open: en
  not not_1 (tunnel_t[7], A);
  assign not_2_out = ~in_1[6:0];  // NOT_Gate not_2, 7 bits wide
  Comparator #(.width(1), .mode("unsigned")) comparator_1 (.a(in_1[7]), .b(1'b1), .eq(A));  // open: gt, lt
  Adder #(.width(7)) adder_1 (.a(7'b0000001), .b(not_2_out), .out(C));  // open: cin, cout
  Multiplexer #(.select(2), .width(8)) multiplexer_3 (
    .in0({8{1'b0}}), .in1({A, tunnel}), .in2(tunnel_t), .in3({8{1'b0}}), .out(out_4), .sel({in_2, in_3}));  // open: en

  // Other names for the same wires on the sheet: B[6:0] = in_1[6:0]; tunnel[7] = A
endmodule
